// Digital circuit ALU.dig as structural Verilog
module ALU (
  input  [7:0] RHS,
  input  [7:0] LHS,
  input  Assert_Main,
  input  [3:0] Control,
  input  Clock,
  output [7:0] MAIN,
  output [4:0] FLAGS
);

  wire Enable, multiplexer_3_out, nor_2_out, or_2_out, xor_1_out, xor_2_out;
  wire [2:2] multiplexer_1_out_2;
  wire [3:0] register_3_q;
  wire [6:0] add_1_s, ALU_Control_out;
  wire [7:0] and_2_out, multiplexer_1_out, multiplexer_2_out, not_2_out, or_1_out, register_1_q,
       register_2_q, xor_3_out;

  not not_1 (Enable, Assert_Main);
  and and_1 (FLAGS[0], xor_2_out, xor_1_out);
  xor xor_1 (xor_1_out, FLAGS[1], multiplexer_1_out[7]);
  xor xor_2 (xor_2_out, multiplexer_2_out[7], FLAGS[1]);
  Multiplexer #(.Selector_Bits(2), .Bits(9)) multiplexer_1 (
    .sel(ALU_Control_out[4:3]), .in_0({FLAGS[4], LHS}), .in_1({LHS[0], FLAGS[4], LHS[7:1]}),
    .in_2({LHS, FLAGS[4]}), .in_3({9{1'b0}}), .out({multiplexer_1_out_2[2], multiplexer_1_out}));
  nor nor_1 (FLAGS[2], add_1_s[0], add_1_s[1], add_1_s[2], add_1_s[3], add_1_s[4], add_1_s[5], add_1_s[6], FLAGS[1]);
  Register #(.Bits(8)) register_1 (.D(multiplexer_1_out), .C(or_2_out), .en(1'b1), .Q(register_1_q));
  Multiplexer #(.Selector_Bits(3), .Bits(8)) multiplexer_2 (
    .sel(ALU_Control_out[2:0]), .in_0({8{1'b0}}), .in_1(not_2_out), .in_2(xor_3_out), .in_3(and_2_out),
    .in_4(RHS), .in_5(or_1_out), .in_6(8'h1), .in_7(8'h1), .out(multiplexer_2_out));
  assign not_2_out = ~RHS;  // Not not_2, 8 bits wide
  assign MAIN = ~Enable ? {FLAGS[1], add_1_s} : 8'bz;  // DriverInvSel driverinvsel_1
  Add #(.Bits(8)) add_1 (
    .a(register_1_q), .b(register_2_q), .c_i(multiplexer_3_out), .s({FLAGS[1], add_1_s}), .c_o(FLAGS[3]));
  Register #(.Bits(8)) register_2 (.D(multiplexer_2_out), .C(or_2_out), .en(1'b1), .Q(register_2_q));
  assign xor_3_out = RHS ^ LHS;  // XOr xor_3, 8 bits wide
  Multiplexer #(.Selector_Bits(2)) multiplexer_3 (
    .sel(register_3_q[1:0]), .in_0(1'b0), .in_1(register_3_q[3]), .in_2(1'b1), .in_3(1'b0),
    .out(multiplexer_3_out));
  assign or_1_out = RHS | LHS;  // Or or_1, 8 bits wide
  assign and_2_out = RHS & LHS;  // And and_2, 8 bits wide
  Register #(.Bits(4)) register_3 (
    .D({FLAGS[3], multiplexer_1_out_2[2], ALU_Control_out[6:5]}), .C(or_2_out), .en(1'b1),
    .Q({register_3_q[3], FLAGS[4], register_3_q[1:0]}));
  LookUpTable #(.Bits(7)) ALU_Control (
    .in0(Control[0]), .in1(Control[1]), .in2(Control[2]), .in3(Control[3]), .out(ALU_Control_out));
  or or_2 (or_2_out, nor_2_out, Clock);
  nor nor_2 (nor_2_out, Control[0], Control[1], Control[2], Control[3]);

  // Other names for the same wires on the sheet: Logical_Carry = FLAGS[4]; Sign = FLAGS[1];
  //   Arithmetic_Carry = FLAGS[3]; LHSBus[7:0] = LHS; MainBus[7:0] = MAIN; Overflow = FLAGS[0]; RHSBus[7:0] = RHS;
  //   Zero = FLAGS[2]

  // Notes on the sheet:
  //   FLAGS: 0: Overflow
  //   1: Sign
  //   2: Zero
  //   3: Carry A
  //   4: Carry L
  //   Control: 0-3: ALUOP0-3
  //   contents of ALU_Control (hex, n*v repeats v):
  //   0,8,10,5,25,f4240,20,1,21,7,1c,1e,1208,1d,18
endmodule
