// Digital circuit Constant Register.dig as structural Verilog
module Constant_Register (
  input  [2:0] Control,
  input  [7:0] MEM,
  output [7:0] MAIN
);

  wire _7400_1_pin2, _7400_1_pin3, _7400_1_pin4, RegValid;

  _74574 _74574_1 (
    .pin1(Control[2]), .pin2(MEM[0]), .pin3(MEM[1]), .pin4(MEM[2]), .pin5(MEM[3]), .pin6(MEM[4]),
    .pin7(MEM[5]), .pin8(MEM[6]), .pin9(MEM[7]), .pin10(1'b0), .pin11(Control[0]), .pin12(MAIN[7]),
    .pin13(MAIN[6]), .pin14(MAIN[5]), .pin15(MAIN[4]), .pin16(MAIN[3]), .pin17(MAIN[2]), .pin18(MAIN[1]),
    .pin19(MAIN[0]), .pin20(1'b1));
  _74574 _74574_2 (
    .pin1(RegValid), .pin2(MEM[0]), .pin3(MEM[1]), .pin4(MEM[2]), .pin5(MEM[3]), .pin6(MEM[4]),
    .pin7(MEM[5]), .pin8(MEM[6]), .pin9(MEM[7]), .pin10(1'b0), .pin11(Control[0]), .pin20(1'b1));  // open: pin12, pin13, pin14, pin15, pin16, pin17, pin18, pin19
  _7400 _7400_1 (
    .pin1(Control[0]), .pin2(_7400_1_pin2), .pin3(_7400_1_pin3), .pin4(_7400_1_pin4), .pin5(_7400_1_pin4),
    .pin6(RegValid), .pin7(1'b0), .pin8(_7400_1_pin4), .pin9(Control[2]), .pin10(1'b0), .pin11(_7400_1_pin2),
    .pin12(_7400_1_pin3), .pin13(Control[2]), .pin14(1'b1));

  // Other names for the same wires on the sheet: MainBus[7:0] = MAIN; Load = Control[0]; A_Main = Control[2];
  //   MemData[7:0] = MEM

  // Notes on the sheet:
  //   Control: 0: Load Bus
  //   1: Load Mem
  //   2: Assert Main, default 1
endmodule
