// Digital circuit Core.dig as structural Verilog
module Core (
  input  Clock,
  input  nReset,
  input  [7:0] D_IN,
  output R_nW,
  output [15:0] Addr,
  output [7:0] D_OUT
);

  wire Break, BusRequest, decoder_1_out_0, decoder_1_out_1, decoder_2_out_1, decoder_2_out_2,
       decoder_2_out_3, decoder_3_out_1, decoder_3_out_2, decoder_3_out_3, decoder_3_out_4, decoder_3_out_5,
       decoder_3_out_6, decoder_3_out_7, decoder_3_out_8, decoder_3_out_9, decoder_3_out_10,
       decoder_3_out_11, decoder_3_out_12, decoder_3_out_13, decoder_3_out_14, decoder_3_out_15,
       decoder_4_out_1, decoder_4_out_2, decoder_4_out_3, decoder_4_out_4, decoder_4_out_6, decoder_4_out_7,
       FetchSuppress, not_1_out, or_1_out, or_2_out, or_3_out, or_4_out, or_5_out, or_6_out, or_7_out;
  wire [1:0] Assert2Main;
  wire [2:0] AddrAssert, Assert2Xfer;
  wire [3:0] AluAssert, AluOp, Inc, LoadMain, LoadXfer_Dec;
  wire [3:2] register_4_q;
  wire [4:0] AluFlags;
  wire [7:0] alu_1_main, GPR_A_q, GPR_B_q, GPR_C_2_q, GPR_C_q, MemData, multiplexer_2_out, multiplexer_4_out,
       multiplexer_5_out, multiplexer_6_out, multiplexer_8_out, register_1_q, register_3_q;
  wire [15:0] _1A_d, _2A_d, counterpreset_1_out, counterpreset_2_out, counterpreset_3_out,
       counterpreset_4_out, counterpreset_5_out, TL_q, Xfer;

  Decoder #(.Selector_Bits(2)) decoder_1 (
    .sel({BusRequest, Inc[0]}), .out_0(decoder_1_out_0), .out_1(decoder_1_out_1));  // open: out_2, out_3
  Decoder #(.Selector_Bits(2)) decoder_2 (
    .sel(Inc[3:2]), .out_1(decoder_2_out_1), .out_2(decoder_2_out_2), .out_3(decoder_2_out_3));  // open: out_0
  Decoder #(.Selector_Bits(4)) decoder_3 (
    .sel(LoadXfer_Dec), .out_1(decoder_3_out_1), .out_2(decoder_3_out_2), .out_3(decoder_3_out_3),
    .out_4(decoder_3_out_4), .out_5(decoder_3_out_5), .out_6(decoder_3_out_6), .out_7(decoder_3_out_7),
    .out_8(decoder_3_out_8), .out_9(decoder_3_out_9), .out_10(decoder_3_out_10), .out_11(decoder_3_out_11),
    .out_12(decoder_3_out_12), .out_13(decoder_3_out_13), .out_14(decoder_3_out_14), .out_15(decoder_3_out_15));  // open: out_0
  or or_1 (or_1_out, decoder_1_out_0, decoder_3_out_9);
  or or_2 (or_2_out, decoder_1_out_1, decoder_3_out_10);
  or or_3 (or_3_out, decoder_2_out_1, decoder_3_out_11);
  or or_4 (or_4_out, decoder_2_out_2, decoder_3_out_12);
  or or_5 (or_5_out, decoder_2_out_3, decoder_3_out_13);
  CounterPreset #(.Bits(16)) counterpreset_1 (
    .en(or_1_out), .C(not_1_out), .dir(decoder_3_out_9), .in(Xfer), .ld(decoder_3_out_1), .clr(nReset),
    .out(counterpreset_1_out));  // open: ovf
  CounterPreset #(.Bits(16)) counterpreset_2 (
    .en(or_2_out), .C(not_1_out), .dir(decoder_3_out_10), .in(Xfer), .ld(decoder_3_out_2), .clr(nReset),
    .out(counterpreset_2_out));  // open: ovf
  CounterPreset #(.Bits(16)) counterpreset_3 (
    .en(or_3_out), .C(not_1_out), .dir(decoder_3_out_11), .in(Xfer), .ld(decoder_3_out_3), .clr(nReset),
    .out(counterpreset_3_out));  // open: ovf
  CounterPreset #(.Bits(16)) counterpreset_4 (
    .en(or_4_out), .C(not_1_out), .dir(decoder_3_out_12), .in(Xfer), .ld(decoder_3_out_4), .clr(nReset),
    .out(counterpreset_4_out));  // open: ovf
  CounterPreset #(.Bits(16)) counterpreset_5 (
    .en(or_5_out), .C(not_1_out), .dir(decoder_3_out_13), .in(Xfer), .ld(decoder_3_out_5), .clr(nReset),
    .out(counterpreset_5_out));  // open: ovf
  not not_1 (not_1_out, Clock);
  Multiplexer #(.Selector_Bits(3), .Bits(16)) multiplexer_1 (
    .sel(AddrAssert), .in_0({16{1'b0}}), .in_1(counterpreset_1_out), .in_2(counterpreset_2_out),
    .in_3(counterpreset_3_out), .in_4(counterpreset_4_out), .in_5(counterpreset_5_out), .in_6(TL_q),
    .in_7({16{1'b0}}), .out(Addr));
  Register #(.Bits(8)) register_1 (.D(MemData), .C(Clock), .en(1'b1), .Q(register_1_q));
  mem_io mem_io_1 (.D_IN(D_OUT), .Addr(Addr), .R_nW(R_nW), .Clock(Clock), .D_OUT(MemData));
  Register #(.Bits(16)) register_2 (
    .D(_1A_d), .C(Clock), .en(1'b1), .Q({FetchSuppress, Assert2Xfer, LoadXfer_Dec, AluOp, AluAssert}));
  ROM #(.AddrBits(15), .Bits(8)) _1A (.A({nReset, Inc[0], AluFlags, multiplexer_2_out}), .sel(1'b1), .D(_1A_d[7:0]));
  Multiplexer #(.Selector_Bits(2), .Bits(8)) multiplexer_2 (
    .sel({BusRequest, FetchSuppress}), .in_0(MemData), .in_1({8{1'b0}}), .in_2({8{1'b0}}),
    .in_3(register_1_q), .out(multiplexer_2_out));
  Multiplexer #(.Selector_Bits(3), .Bits(16)) multiplexer_3 (
    .sel(Assert2Xfer), .in_0({16{1'b0}}), .in_1(counterpreset_1_out), .in_2(counterpreset_2_out),
    .in_3(counterpreset_3_out), .in_4(counterpreset_4_out), .in_5(counterpreset_5_out), .in_6(TL_q),
    .in_7({16{1'b0}}), .out(Xfer));
  ROM #(.AddrBits(15), .Bits(8)) _1B (.A({nReset, Inc[0], AluFlags, multiplexer_2_out}), .sel(1'b1), .D(_1A_d[15:8]));
  Register #(.Bits(8)) register_3 (.D(multiplexer_2_out), .C(Clock), .en(1'b1), .Q(register_3_q));
  Decoder #(.Selector_Bits(4)) decoder_4 (
    .sel(LoadMain), .out_1(decoder_4_out_1), .out_2(decoder_4_out_2), .out_3(decoder_4_out_3),
    .out_4(decoder_4_out_4), .out_6(decoder_4_out_6), .out_7(decoder_4_out_7), .out_15(R_nW));  // open: out_0, out_5, out_8, out_9, out_10, out_11, out_12, out_13, out_14
  Register #(.Bits(16)) register_4 (
    .D(_2A_d), .C(Clock), .en(1'b1),
    .Q({Break, Inc[0], BusRequest, AddrAssert, Inc[3:2], LoadMain, register_4_q, Assert2Main}));
  ROM #(.AddrBits(15), .Bits(8)) _2A (.A({nReset, Inc[0], AluFlags, register_3_q}), .sel(1'b1), .D(_2A_d[7:0]));
  ROM #(.AddrBits(15), .Bits(8)) _2B (.A({nReset, Inc[0], AluFlags, register_3_q}), .sel(1'b1), .D(_2A_d[15:8]));
  or or_6 (or_6_out, decoder_4_out_6, decoder_3_out_6);
  or or_7 (or_7_out, decoder_4_out_7, decoder_3_out_6);
  // Probe P2 on register_3_q
  // Probe P1 on multiplexer_2_out
  // Probe Flags on {nReset, Inc[0], AluFlags}
  Multiplexer #(.Bits(8)) multiplexer_4 (
    .sel(decoder_3_out_6), .in_0(D_OUT), .in_1(Xfer[7:0]), .out(multiplexer_4_out));
  Multiplexer #(.Bits(8)) multiplexer_5 (
    .sel(decoder_3_out_6), .in_0(D_OUT), .in_1(Xfer[15:8]), .out(multiplexer_5_out));
  Register #(.Bits(8)) GPR_A (.D(D_OUT), .C(not_1_out), .en(decoder_4_out_1), .Q(GPR_A_q));
  Register #(.Bits(8)) GPR_B (.D(D_OUT), .C(not_1_out), .en(decoder_4_out_2), .Q(GPR_B_q));
  Register #(.Bits(8)) GPR_C (.D(D_OUT), .C(not_1_out), .en(decoder_4_out_3), .Q(GPR_C_q));
  Register #(.Bits(8)) GPR_C_2 (.D(D_OUT), .C(not_1_out), .en(decoder_4_out_4), .Q(GPR_C_2_q));
  Register #(.Bits(8)) TL (.D(multiplexer_4_out), .C(not_1_out), .en(or_6_out), .Q(TL_q[7:0]));
  Register #(.Bits(8)) TH (.D(multiplexer_5_out), .C(not_1_out), .en(or_7_out), .Q(TL_q[15:8]));
  ALU alu_1 (
    .RHS(multiplexer_8_out), .LHS(multiplexer_6_out), .MAIN(alu_1_main), .FLAGS(AluFlags), .Clock(not_1_out),
    .Control(AluOp));
  // Probe on Assert2Xfer
  // Probe on LoadXfer_Dec
  Multiplexer #(.Selector_Bits(2), .Bits(8)) multiplexer_6 (
    .sel(AluAssert[1:0]), .in_0(GPR_A_q), .in_1(GPR_B_q), .in_2(GPR_C_q), .in_3(GPR_C_2_q),
    .out(multiplexer_6_out));
  Multiplexer #(.Selector_Bits(2), .Bits(8)) multiplexer_7 (
    .sel(Assert2Main), .in_0(alu_1_main), .in_1(TL_q[7:0]), .in_2(TL_q[15:8]), .in_3(MemData), .out(D_OUT));
  Multiplexer #(.Selector_Bits(2), .Bits(8)) multiplexer_8 (
    .sel(AluAssert[3:2]), .in_0(GPR_A_q), .in_1(GPR_B_q), .in_2(GPR_C_q), .in_3(GPR_C_2_q),
    .out(multiplexer_8_out));
  // Probe Mem on MemData
  // Probe Main on D_OUT
  // Probe Addr on Addr
  // Probe Xfer on Xfer

  // Other names for the same wires on the sheet: Inc[1] = BusRequest; PCRAFlip = Inc[0]; Main[7:0] = D_OUT;
  //   Reset = nReset

  // Notes on the sheet:
  //   Clock: Hz: 1000
  //   nReset: default 1
  //   contents of _1A (hex, n*v repeats v):
  //   0,0,0,0,0,0,0,0,0,0,0,0,0,0,0,0,0,0,0,0,0,0,0,0,0,0,0,0,0,0,0,0,0,0,0,0,0,0,0,0,0,
  //   0,0,0,0,0,0,0,0,0,0,0,0,0,0,0,0,0,0,0,0,0,0,0,0,0,0,0,0,0,0,0,0,0,0,0,0,0,0,0,0,0,
  //   0,0,0,0,0,0,0,0,0,0,0,0,0,0,0,0,0,0,0,0,0,0,0,0,0,0,0,0,0,0,0,0,0,0,0,0,0,0,0,0,0,
  //   0,0,0,0,e0,10,15,1a,1f,20,25,2a,2f,34,38,3c,31,39,3d,32,36,3e,33,37,3b,44,48,4c,41,
  //   49,4d,42,46,4e,43,47,4b,50,55,5a,5f,60,65,6a,6f,74,78,7c,71,79,7d,72,76,7e,73,77,
  //   7b,84,88,8c,81,89,8d,82,86,8e,83,87,8b,90,95,9a,9f,a4,a8,ac,a1,a9,ad,a2,a6,ae,a3,
  //   a7,ab,b4,b8,bc,b1,b9,bd,b2,b6,be,b3,b7,bb,c4,c8,cc,c1,c9,cd,c2,c6,ce,c3,c7,cb,c0,
  //   c5,ca,cf,d0,d5,da,df,74,78,7c,71,79,7d,72,76,7e,73,77,7b,a0,a5,aa,af,0,0,0,0,0,0,
  //   0,0,0,0,0,0,0,0,0,0,0,0,0,0,0,0,0,0,0,0,0,0,0,0,0,0,0,0,0,0,0,0,0,0,0,0,0,0,0,0,0,
  //   0,0,0,0,0,0,0,0,0,0,0,0,0,0,0,0,0,0,0,0,0,0,0,0,0,0,0,0,0,0,0,0,0,0,0,0,0,0,0,0,0,
  //   0,0,0,0,0,0,0,0,0,0,0,0,0,0,0,0,0,0,0,0,0,0,0,0,0,0,0,0,0,0,0,0,0,0,0,0,0,0,0,e0,
  //   10,15,1a,1f,20,25,2a,2f,34,38,3c,31,39,3d,32,36,3e,33,37,3b,44,48,4c,41,49,4d,42,
  //   46,4e,43,47,4b,50,55,5a,5f,60,65,6a,6f,74,78,7c,71,79,7d,72,76,7e,73,77,7b,84,88,
  //   8c,81,89,8d,82,86,8e,83,87,8b,90,95,9a,9f,a4,a8,ac,a1,a9,ad,a2,a6,ae,a3,a7,ab,b4,
  //   b8,bc,b1,b9,bd,b2,b6,be,b3,b7,bb,c4,c8,cc,c1,c9,cd,c2,c6,ce,c3,c7,cb,c0,c5,ca,cf,
  //   d0,d5,da,df,74,78,7c,71,79,7d,72,76,7e,73,77,7b,a0,a5,aa,af,0,0,0,0,0,0,0,0,0,0,0,
  //   0,0,0,0,0,0,0,0,0,0,0,0,0,0,0,0,0,0,0,0,0,0,0,0,0,0,0,0,0,0,0,0,0,0,0,0,0,0,0,0,0,
  //   0,0,0,0,0,0,0,0,0,0,0,0,0,0,0,0,0,0,0,0,0,0,0,0,0,0,0,0,0,0,0,0,0,0,0,0,0,0,0,0,0,
  //   0,0,0,0,0,0,0,0,0,0,0,0,0,0,0,0,0,0,0,0,0,0,0,0,0,0,0,0,0,0,0,0,0,0,e0,10,15,1a,1f,
  //   20,25,2a,2f,34,38,3c,31,39,3d,32,36,3e,33,37,3b,44,48,4c,41,49,4d,42,46,4e,43,47,
  //   4b,50,55,5a,5f,60,65,6a,6f,74,78,7c,71,79,7d,72,76,7e,73,77,7b,84,88,8c,81,89,8d,
  //   82,86,8e,83,87,8b,90,95,9a,9f,a4,a8,ac,a1,a9,ad,a2,a6,ae,a3,a7,ab,b4,b8,bc,b1,b9,
  //   bd,b2,b6,be,b3,b7,bb,c4,c8,cc,c1,c9,cd,c2,c6,ce,c3,c7,cb,c0,c5,ca,cf,d0,d5,da,df,
  //   74,78,7c,71,79,7d,72,76,7e,73,77,7b,a0,a5,aa,af,0,0,0,0,0,0,0,0,0,0,0,0,0,0,0,0,0,
  //   0,0,0,0,0,0,0,0,0,0,0,0,0,0,0,0,0,0,0,0,0,0,0,0,0,0,0,0,0,0,0,0,0,0,0,0,0,0,0,0,0,
  //   0,0,0,0,0,0,0,0,0,0,0,0,0,0,0,0,0,0,0,0,0,0,0,0,0,0,0,0,0,0,0,0,0,0,0,0,0,0,0,0,0,
  //   0,0,0,0,0,0,0,0,0,0,0,0,0,0,0,0,0,0,0,0,0,0,0,0,0,0,0,0,e0,10,15,1a,1f,20,25,2a,2f,
  //   34,38,3c,31,39,3d,32,36,3e,33,37,3b,44,48,4c,41,49,4d,42,46,4e,43,47,4b,50,55,5a,
  //   5f,60,65,6a,6f,74,78,7c,71,79,7d,72,76,7e,73,77,7b,84,88,8c,81,89,8d,82,86,8e,83,
  //   87,8b,90,95,9a,9f,a4,a8,ac,a1,a9,ad,a2,a6,ae,a3,a7,ab,b4,b8,bc,b1,b9,bd,b2,b6,be,
  //   b3,b7,bb,c4,c8,cc,c1,c9,cd,c2,c6,ce,c3,c7,cb,c0,c5,ca,cf,d0,d5,da,df,74,78,7c,71,
  //   79,7d,72,76,7e,73,77,7b,a0,a5,aa,af,0,0,0,0,0,0,0,0,0,0,0,0,0,0,0,0,0,0,0,0,0,0,0,
  //   0,0,0,0,0,0,0,0,0,0,0,0,0,0,0,0,0,0,0,0,0,0,0,0,0,0,0,0,0,0,0,0,0,0,0,0,0,0,0,0,0,
  //   0,0,0,0,0,0,0,0,0,0,0,0,0,0,0,0,0,0,0,0,0,0,0,0,0,0,0,0,0,0,0,0,0,0,0,0,0,0,0,0,0,
  //   0,0,0,0,0,0,0,0,0,0,0,0,0,0,0,0,0,0,0,0,0,0,e0,10,15,1a,1f,20,25,2a,2f,34,38,3c,31,
  //   39,3d,32,36,3e,33,37,3b,44,48,4c,41,49,4d,42,46,4e,43,47,4b,50,55,5a,5f,60,65,6a,
  //   6f,74,78,7c,71,79,7d,72,76,7e,73,77,7b,84,88,8c,81,89,8d,82,86,8e,83,87,8b,90,95,
  //   9a,9f,a4,a8,ac,a1,a9,ad,a2,a6,ae,a3,a7,ab,b4,b8,bc,b1,b9,bd,b2,b6,be,b3,b7,bb,c4,
  //   c8,cc,c1,c9,cd,c2,c6,ce,c3,c7,cb,c0,c5,ca,cf,d0,d5,da,df,74,78,7c,71,79,7d,72,76,
  //   7e,73,77,7b,a0,a5,aa,af,0,0,0,0,0,0,0,0,0,0,0,0,0,0,0,0,0,0,0,0,0,0,0,0,0,0,0,0,0,
  //   0,0,0,0,0,0,0,0,0,0,0,0,0,0,0,0,0,0,0,0,0,0,0,0,0,0,0,0,0,0,0,0,0,0,0,0,0,0,0,0,0,
  //   0,0,0,0,0,0,0,0,0,0,0,0,0,0,0,0,0,0,0,0,0,0,0,0,0,0,0,0,0,0,0,0,0,0,0,0,0,0,0,0,0,
  //   0,0,0,0,0,0,0,0,0,0,0,0,0,0,0,0,e0,10,15,1a,1f,20,25,2a,2f,34,38,3c,31,39,3d,32,36,
  //   3e,33,37,3b,44,48,4c,41,49,4d,42,46,4e,43,47,4b,50,55,5a,5f,60,65,6a,6f,74,78,7c,
  //   71,79,7d,72,76,7e,73,77,7b,84,88,8c,81,89,8d,82,86,8e,83,87,8b,90,95,9a,9f,a4,a8,
  //   ac,a1,a9,ad,a2,a6,ae,a3,a7,ab,b4,b8,bc,b1,b9,bd,b2,b6,be,b3,b7,bb,c4,c8,cc,c1,c9,
  //   cd,c2,c6,ce,c3,c7,cb,c0,c5,ca,cf,d0,d5,da,df,74,78,7c,71,79,7d,72,76,7e,73,77,7b,
  //   a0,a5,aa,af,0,0,0,0,0,0,0,0,0,0,0,0,0,0,0,0,0,0,0,0,0,0,0,0,0,0,0,0,0,0,0,0,0,0,0,
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  //   contents of _1B (hex, n*v repeats v):
  //   0,80,80,80,80,80,80,0,0,0,0,0,0,0,0,0,0,0,0,0,0,0,0,0,0,0,0,0,0,0,0,0,0,0,0,62,26,
  //   63,36,64,46,65,56,45,54,34,35,0,a,b,c,d,0,0,0,0,0,0,0,0,0,0,0,0,0,0,0,0,0,0,0,0,0,
  //   0,0,0,0,0,0,0,0,0,0,0,0,0,0,0,0,0,0,0,62,52,0,0,61,0,61,0,61,0,61,0,61,0,61,0,61,
  //   0,61,0,61,51,b,b,b,b,b,b,0,0,0,0,0,0,0,0,0,0,0,0,0,0,0,0,0,0,0,0,0,0,0,0,0,0,0,0,
  //   0,0,0,0,0,0,0,0,0,0,0,0,0,0,0,0,0,0,0,0,0,0,0,0,0,0,0,0,0,0,0,0,0,0,0,0,0,0,0,0,0,
  //   0,0,0,0,0,0,0,0,0,0,0,0,0,0,0,0,0,0,0,0,0,0,0,0,0,0,0,0,0,0,0,0,0,0,0,0,0,0,0,0,0,
  //   0,0,0,0,0,0,0,0,0,0,0,0,0,0,0,0,0,0,0,0,0,0,0,0,0,0,0,80,80,80,80,80,80,0,0,0,0,0,
  //   0,0,0,0,0,0,0,0,0,0,0,0,0,0,0,0,0,0,0,0,0,0,0,62,26,63,36,64,46,65,56,45,54,34,35,
  //   0,a,b,c,d,0,0,0,0,0,0,0,0,0,0,0,0,0,0,0,0,0,0,0,0,0,0,0,0,0,0,0,0,0,0,0,0,0,0,0,0,
  //   0,0,0,0,62,52,0,0,61,61,0,0,61,0,61,0,61,0,61,61,0,61,61,0,61,51,b,b,b,b,b,b,0,0,
  //   0,0,0,0,0,0,0,0,0,0,0,0,0,0,0,0,0,0,0,0,0,0,0,0,0,0,0,0,0,0,0,0,0,0,0,0,0,0,0,0,0,
  //   0,0,0,0,0,0,0,0,0,0,0,0,0,0,0,0,0,0,0,0,0,0,0,0,0,0,0,0,0,0,0,0,0,0,0,0,0,0,0,0,0,
  //   0,0,0,0,0,0,0,0,0,0,0,0,0,0,0,0,0,0,0,0,0,0,0,0,0,0,0,0,0,0,0,0,0,0,0,0,0,0,0,0,0,
  //   0,0,0,0,0,0,0,0,0,0,0,0,80,80,80,80,80,80,0,0,0,0,0,0,0,0,0,0,0,0,0,0,0,0,0,0,0,0,
  //   0,0,0,0,0,0,0,0,62,26,63,36,64,46,65,56,45,54,34,35,0,a,b,c,d,0,0,0,0,0,0,0,0,0,0,
  //   0,0,0,0,0,0,0,0,0,0,0,0,0,0,0,0,0,0,0,0,0,0,0,0,0,0,0,0,0,0,62,52,0,0,61,0,61,61,
  //   0,0,61,0,61,0,61,61,0,61,0,0,61,51,b,b,b,b,b,b,0,0,0,0,0,0,0,0,0,0,0,0,0,0,0,0,0,
  //   0,0,0,0,0,0,0,0,0,0,0,0,0,0,0,0,0,0,0,0,0,0,0,0,0,0,0,0,0,0,0,0,0,0,0,0,0,0,0,0,0,
  //   0,0,0,0,0,0,0,0,0,0,0,0,0,0,0,0,0,0,0,0,0,0,0,0,0,0,0,0,0,0,0,0,0,0,0,0,0,0,0,0,0,
  //   0,0,0,0,0,0,0,0,0,0,0,0,0,0,0,0,0,0,0,0,0,0,0,0,0,0,0,0,0,0,0,0,0,0,0,0,0,0,80,80,
  //   80,80,80,80,0,0,0,0,0,0,0,0,0,0,0,0,0,0,0,0,0,0,0,0,0,0,0,0,0,0,0,0,62,26,63,36,64,
  //   46,65,56,45,54,34,35,0,a,b,c,d,0,0,0,0,0,0,0,0,0,0,0,0,0,0,0,0,0,0,0,0,0,0,0,0,0,
  //   0,0,0,0,0,0,0,0,0,0,0,0,0,0,0,62,52,0,0,61,61,0,61,0,0,61,0,61,0,61,0,61,0,0,0,61,
  //   51,b,b,b,b,b,b,0,0,0,0,0,0,0,0,0,0,0,0,0,0,0,0,0,0,0,0,0,0,0,0,0,0,0,0,0,0,0,0,0,
  //   0,0,0,0,0,0,0,0,0,0,0,0,0,0,0,0,0,0,0,0,0,0,0,0,0,0,0,0,0,0,0,0,0,0,0,0,0,0,0,0,0,
  //   0,0,0,0,0,0,0,0,0,0,0,0,0,0,0,0,0,0,0,0,0,0,0,0,0,0,0,0,0,0,0,0,0,0,0,0,0,0,0,0,0,
  //   0,0,0,0,0,0,0,0,0,0,0,0,0,0,0,0,0,0,0,0,0,0,80,80,80,80,80,80,0,0,0,0,0,0,0,0,0,0,
  //   0,0,0,0,0,0,0,0,0,0,0,0,0,0,0,0,0,0,62,26,63,36,64,46,65,56,45,54,34,35,0,a,b,c,d,
  //   0,0,0,0,0,0,0,0,0,0,0,0,0,0,0,0,0,0,0,0,0,0,0,0,0,0,0,0,0,0,0,0,0,0,0,0,0,0,0,0,62,
  //   52,0,0,61,0,61,0,61,61,0,0,61,61,0,0,61,61,0,0,61,51,b,b,b,b,b,b,0,0,0,0,0,0,0,0,
  //   0,0,0,0,0,0,0,0,0,0,0,0,0,0,0,0,0,0,0,0,0,0,0,0,0,0,0,0,0,0,0,0,0,0,0,0,0,0,0,0,0,
  //   0,0,0,0,0,0,0,0,0,0,0,0,0,0,0,0,0,0,0,0,0,0,0,0,0,0,0,0,0,0,0,0,0,0,0,0,0,0,0,0,0,
  //   0,0,0,0,0,0,0,0,0,0,0,0,0,0,0,0,0,0,0,0,0,0,0,0,0,0,0,0,0,0,0,0,0,0,0,0,0,0,0,0,0,
  //   0,0,0,0,0,0,80,80,80,80,80,80,0,0,0,0,0,0,0,0,0,0,0,0,0,0,0,0,0,0,0,0,0,0,0,0,0,0,
  //   0,0,62,26,63,36,64,46,65,56,45,54,34,35,0,a,b,c,d,0,0,0,0,0,0,0,0,0,0,0,0,0,0,0,0,
  //   0,0,0,0,0,0,0,0,0,0,0,0,0,0,0,0,0,0,0,0,0,0,0,0,62,52,0,0,61,61,0,0,61,61,0,0,61,
  //   61,0,61,0,61,0,0,61,51,b,b,b,b,b,b,0,0,0,0,0,0,0,0,0,0,0,0,0,0,0,0,0,0,0,0,0,0,0,
  //   0,0,0,0,0,0,0,0,0,0,0,0,0,0,0,0,0,0,0,0,0,0,0,0,0,0,0,0,0,0,0,0,0,0,0,0,0,0,0,0,0,
  //   0,0,0,0,0,0,0,0,0,0,0,0,0,0,0,0,0,0,0,0,0,0,0,0,0,0,0,0,0,0,0,0,0,0,0,0,0,0,0,0,0,
  //   0,0,0,0,0,0,0,0,0,0,0,0,0,0,0,0,0,0,0,0,0,0,0,0,0,0,0,0,0,0,0,0,80,80,80,80,80,80,
  //   0,0,0,0,0,0,0,0,0,0,0,0,0,0,0,0,0,0,0,0,0,0,0,0,0,0,0,0,62,26,63,36,64,46,65,56,45,
  //   54,34,35,0,a,b,c,d,0,0,0,0,0,0,0,0,0,0,0,0,0,0,0,0,0,0,0,0,0,0,0,0,0,0,0,0,0,0,0,
  //   0,0,0,0,0,0,0,0,0,62,52,0,0,61,0,61,61,0,61,0,0,61,61,0,61,0,61,0,0,61,51,b,b,b,b,
  //   b,b,0,0,0,0,0,0,0,0,0,0,0,0,0,0,0,0,0,0,0,0,0,0,0,0,0,0,0,0,0,0,0,0,0,0,0,0,0,0,0,
  //   0,0,0,0,0,0,0,0,0,0,0,0,0,0,0,0,0,0,0,0,0,0,0,0,0,0,0,0,0,0,0,0,0,0,0,0,0,0,0,0,0,
  //   0,0,0,0,0,0,0,0,0,0,0,0,0,0,0,0,0,0,0,0,0,0,0,0,0,0,0,0,0,0,0,0,0,0,0,0,0,0,0,0,0,
  //   0,0,0,0,0,0,0,0,0,0,0,0,0,0,0,0,80,80,80,80,80,80,0,0,0,0,0,0,0,0,0,0,0,0,0,0,0,0,
  //   0,0,0,0,0,0,0,0,0,0,0,0,62,26,63,36,64,46,65,56,45,54,34,35,0,a,b,c,d,0,0,0,0,0,0,
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  //   contents of _2A (hex, n*v repeats v):
  //   0,13,23,33,43,63,73,10,10,10,20,20,20,30,30,30,40,40,40,60,60,60,60,70,70,70,70,11,
  //   21,31,41,12,22,32,42,0,0,0,0,0,0,0,0,0,0,0,0,0,0,0,0,0,0,0,0,0,0,0,0,0,0,0,0,0,13,
  //   23,33,43,13,23,33,43,13,23,33,43,f0,f0,f0,f0,f0,f0,f0,f0,f0,f0,f0,f0,0,0,0,13,0,0,
  //   0,0,0,0,0,0,0,0,0,0,0,0,0,0,0,0,0,0,0,0,f0,f0,f0,f0,f1,f2,13,23,33,43,63,73,f0,0,
  //   10,20,30,40,10,20,30,40,10,10,10,20,20,20,30,30,30,40,40,40,10,10,10,20,20,20,30,
  //   30,30,40,40,40,10,20,30,40,10,20,30,40,10,10,10,20,20,20,30,30,30,40,40,40,10,10,
  //   10,20,20,20,30,30,30,40,40,40,10,20,30,40,10,10,10,20,20,20,30,30,30,40,40,40,10,
  //   10,10,20,20,20,30,30,30,40,40,40,10,10,10,20,20,20,30,30,30,40,40,40,10,20,30,40,
  //   10,20,30,40,0,0,0,0,0,0,0,0,0,0,0,0,0,0,0,0,0,13,23,33,43,63,73,10,10,10,20,20,20,
  //   30,30,30,40,40,40,60,60,60,60,70,70,70,70,11,21,31,41,12,22,32,42,0,0,0,0,0,0,0,0,
  //   0,0,0,0,0,0,0,0,0,0,0,0,0,0,0,0,0,0,0,0,0,13,23,33,43,13,23,33,43,13,23,33,43,f0,
  //   f0,f0,f0,f0,f0,f0,f0,f0,f0,f0,f0,0,0,0,13,0,0,0,0,0,0,0,0,0,0,0,0,0,0,0,0,0,0,0,0,
  //   0,0,f0,f0,f0,f0,f1,f2,13,23,33,43,63,73,f0,0,10,20,30,40,10,20,30,40,10,10,10,20,
  //   20,20,30,30,30,40,40,40,10,10,10,20,20,20,30,30,30,40,40,40,10,20,30,40,10,20,30,
  //   40,10,10,10,20,20,20,30,30,30,40,40,40,10,10,10,20,20,20,30,30,30,40,40,40,10,20,
  //   30,40,10,10,10,20,20,20,30,30,30,40,40,40,10,10,10,20,20,20,30,30,30,40,40,40,10,
  //   10,10,20,20,20,30,30,30,40,40,40,10,20,30,40,10,20,30,40,0,0,0,0,0,0,0,0,0,0,0,0,
  //   0,0,0,0,0,13,23,33,43,63,73,10,10,10,20,20,20,30,30,30,40,40,40,60,60,60,60,70,70,
  //   70,70,11,21,31,41,12,22,32,42,0,0,0,0,0,0,0,0,0,0,0,0,0,0,0,0,0,0,0,0,0,0,0,0,0,0,
  //   0,0,0,13,23,33,43,13,23,33,43,13,23,33,43,f0,f0,f0,f0,f0,f0,f0,f0,f0,f0,f0,f0,0,0,
  //   0,13,0,0,0,0,0,0,0,0,0,0,0,0,0,0,0,0,0,0,0,0,0,0,f0,f0,f0,f0,f1,f2,13,23,33,43,63,
  //   73,f0,0,10,20,30,40,10,20,30,40,10,10,10,20,20,20,30,30,30,40,40,40,10,10,10,20,20,
  //   20,30,30,30,40,40,40,10,20,30,40,10,20,30,40,10,10,10,20,20,20,30,30,30,40,40,40,
  //   10,10,10,20,20,20,30,30,30,40,40,40,10,20,30,40,10,10,10,20,20,20,30,30,30,40,40,
  //   40,10,10,10,20,20,20,30,30,30,40,40,40,10,10,10,20,20,20,30,30,30,40,40,40,10,20,
  //   30,40,10,20,30,40,0,0,0,0,0,0,0,0,0,0,0,0,0,0,0,0,0,13,23,33,43,63,73,10,10,10,20,
  //   20,20,30,30,30,40,40,40,60,60,60,60,70,70,70,70,11,21,31,41,12,22,32,42,0,0,0,0,0,
  //   0,0,0,0,0,0,0,0,0,0,0,0,0,0,0,0,0,0,0,0,0,0,0,0,13,23,33,43,13,23,33,43,13,23,33,
  //   43,f0,f0,f0,f0,f0,f0,f0,f0,f0,f0,f0,f0,0,0,0,13,0,0,0,0,0,0,0,0,0,0,0,0,0,0,0,0,0,
  //   0,0,0,0,0,f0,f0,f0,f0,f1,f2,13,23,33,43,63,73,f0,0,10,20,30,40,10,20,30,40,10,10,
  //   10,20,20,20,30,30,30,40,40,40,10,10,10,20,20,20,30,30,30,40,40,40,10,20,30,40,10,
  //   20,30,40,10,10,10,20,20,20,30,30,30,40,40,40,10,10,10,20,20,20,30,30,30,40,40,40,
  //   10,20,30,40,10,10,10,20,20,20,30,30,30,40,40,40,10,10,10,20,20,20,30,30,30,40,40,
  //   40,10,10,10,20,20,20,30,30,30,40,40,40,10,20,30,40,10,20,30,40,0,0,0,0,0,0,0,0,0,
  //   0,0,0,0,0,0,0,0,13,23,33,43,63,73,10,10,10,20,20,20,30,30,30,40,40,40,60,60,60,60,
  //   70,70,70,70,11,21,31,41,12,22,32,42,0,0,0,0,0,0,0,0,0,0,0,0,0,0,0,0,0,0,0,0,0,0,0,
  //   0,0,0,0,0,0,13,23,33,43,13,23,33,43,13,23,33,43,f0,f0,f0,f0,f0,f0,f0,f0,f0,f0,f0,
  //   f0,0,0,0,13,0,0,0,0,0,0,0,0,0,0,0,0,0,0,0,0,0,0,0,0,0,0,f0,f0,f0,f0,f1,f2,13,23,33,
  //   43,63,73,f0,0,10,20,30,40,10,20,30,40,10,10,10,20,20,20,30,30,30,40,40,40,10,10,10,
  //   20,20,20,30,30,30,40,40,40,10,20,30,40,10,20,30,40,10,10,10,20,20,20,30,30,30,40,
  //   40,40,10,10,10,20,20,20,30,30,30,40,40,40,10,20,30,40,10,10,10,20,20,20,30,30,30,
  //   40,40,40,10,10,10,20,20,20,30,30,30,40,40,40,10,10,10,20,20,20,30,30,30,40,40,40,
  //   10,20,30,40,10,20,30,40,0,0,0,0,0,0,0,0,0,0,0,0,0,0,0,0,0,13,23,33,43,63,73,10,10,
  //   10,20,20,20,30,30,30,40,40,40,60,60,60,60,70,70,70,70,11,21,31,41,12,22,32,42,0,0,
  //   0,0,0,0,0,0,0,0,0,0,0,0,0,0,0,0,0,0,0,0,0,0,0,0,0,0,0,13,23,33,43,13,23,33,43,13,
  //   23,33,43,f0,f0,f0,f0,f0,f0,f0,f0,f0,f0,f0,f0,0,0,0,13,0,0,0,0,0,0,0,0,0,0,0,0,0,0,
  //   0,0,0,0,0,0,0,0,f0,f0,f0,f0,f1,f2,13,23,33,43,63,73,f0,0,10,20,30,40,10,20,30,40,
  //   10,10,10,20,20,20,30,30,30,40,40,40,10,10,10,20,20,20,30,30,30,40,40,40,10,20,30,
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  //   contents of _2B (hex, n*v repeats v):
  //   4,4,4,4,4,4,4,4,4,4,4,4,4,4,4,4,4,4,4,4,4,4,4,4,4,4,4,4,4,4,4,4,4,4,4,4,4,4,4,4,4,
  //   4,4,4,4,4,4,4,4,4,4,4,5,6,7,4,4,4,4,4,4,4,4,4,30,30,30,30,34,34,34,34,38,38,38,38,
  //   30,30,30,30,34,34,34,34,38,38,38,38,4,4,4,32,48,48,48,24,4,4,4,4,4,4,4,4,4,4,4,4,
  //   4,4,4,4,4,4,2c,2c,2c,2c,2c,2c,2d,2d,2d,2d,2d,2d,37,4,4,4,4,4,4,4,4,4,4,4,4,4,4,4,
  //   4,4,4,4,4,4,4,4,4,4,4,4,4,4,4,4,4,4,4,4,4,4,4,4,4,4,4,4,4,4,4,4,4,4,4,4,4,4,4,4,4,
  //   4,4,4,4,4,4,4,4,4,4,4,4,4,4,4,4,4,4,4,4,4,4,4,4,4,4,4,4,4,4,4,4,4,4,4,4,4,4,4,4,4,
  //   4,4,4,4,4,4,4,4,4,4,4,4,4,4,4,4,4,4,4,4,4,4,4,4,4,4,4,4,4,4,4,4,4,4,4,4,4,4,4,4,4,
  //   4,4,4,4,4,4,4,4,4,4,4,4,4,4,4,4,4,4,4,4,4,4,4,4,4,4,4,4,4,4,4,4,4,4,4,4,4,4,4,4,4,
  //   4,4,5,6,7,4,4,4,4,4,4,4,4,4,30,30,30,30,34,34,34,34,38,38,38,38,30,30,30,30,34,34,
  //   34,34,38,38,38,38,4,4,4,32,48,48,48,24,4,4,4,4,4,4,4,4,4,4,4,4,4,4,4,4,4,4,2c,2c,
  //   2c,2c,2c,2c,2d,2d,2d,2d,2d,2d,37,4,4,4,4,4,4,4,4,4,4,4,4,4,4,4,4,4,4,4,4,4,4,4,4,
  //   4,4,4,4,4,4,4,4,4,4,4,4,4,4,4,4,4,4,4,4,4,4,4,4,4,4,4,4,4,4,4,4,4,4,4,4,4,4,4,4,4,
  //   4,4,4,4,4,4,4,4,4,4,4,4,4,4,4,4,4,4,4,4,4,4,4,4,4,4,4,4,4,4,4,4,4,4,4,4,4,4,4,4,4,
  //   4,4,4,4,4,4,4,4,4,4,4,4,4,4,4,4,4,4,4,4,4,4,4,4,4,4,4,4,4,4,4,4,4,4,4,4,4,4,4,4,4,
  //   4,4,4,4,4,4,4,4,4,4,4,4,4,4,4,4,4,4,4,4,4,4,4,4,4,4,4,4,4,4,4,4,4,4,5,6,7,4,4,4,4,
  //   4,4,4,4,4,30,30,30,30,34,34,34,34,38,38,38,38,30,30,30,30,34,34,34,34,38,38,38,38,
  //   4,4,4,32,48,48,48,24,4,4,4,4,4,4,4,4,4,4,4,4,4,4,4,4,4,4,2c,2c,2c,2c,2c,2c,2d,2d,
  //   2d,2d,2d,2d,37,4,4,4,4,4,4,4,4,4,4,4,4,4,4,4,4,4,4,4,4,4,4,4,4,4,4,4,4,4,4,4,4,4,
  //   4,4,4,4,4,4,4,4,4,4,4,4,4,4,4,4,4,4,4,4,4,4,4,4,4,4,4,4,4,4,4,4,4,4,4,4,4,4,4,4,4,
  //   4,4,4,4,4,4,4,4,4,4,4,4,4,4,4,4,4,4,4,4,4,4,4,4,4,4,4,4,4,4,4,4,4,4,4,4,4,4,4,4,4,
  //   4,4,4,4,4,4,4,4,4,4,4,4,4,4,4,4,4,4,4,4,4,4,4,4,4,4,4,4,4,4,4,4,4,4,4,4,4,4,4,4,4,
  //   4,4,4,4,4,4,4,4,4,4,4,4,4,4,4,4,4,4,4,4,4,4,4,4,4,5,6,7,4,4,4,4,4,4,4,4,4,30,30,30,
  //   30,34,34,34,34,38,38,38,38,30,30,30,30,34,34,34,34,38,38,38,38,4,4,4,32,48,48,48,
  //   24,4,4,4,4,4,4,4,4,4,4,4,4,4,4,4,4,4,4,2c,2c,2c,2c,2c,2c,2d,2d,2d,2d,2d,2d,37,4,4,
  //   4,4,4,4,4,4,4,4,4,4,4,4,4,4,4,4,4,4,4,4,4,4,4,4,4,4,4,4,4,4,4,4,4,4,4,4,4,4,4,4,4,
  //   4,4,4,4,4,4,4,4,4,4,4,4,4,4,4,4,4,4,4,4,4,4,4,4,4,4,4,4,4,4,4,4,4,4,4,4,4,4,4,4,4,
  //   4,4,4,4,4,4,4,4,4,4,4,4,4,4,4,4,4,4,4,4,4,4,4,4,4,4,4,4,4,4,4,4,4,4,4,4,4,4,4,4,4,
  //   4,4,4,4,4,4,4,4,4,4,4,4,4,4,4,4,4,4,4,4,4,4,4,4,4,4,4,4,4,4,4,4,4,4,4,4,4,4,4,4,4,
  //   4,4,4,4,4,4,4,4,4,4,4,4,4,4,4,5,6,7,4,4,4,4,4,4,4,4,4,30,30,30,30,34,34,34,34,38,
  //   38,38,38,30,30,30,30,34,34,34,34,38,38,38,38,4,4,4,32,48,48,48,24,4,4,4,4,4,4,4,4,
  //   4,4,4,4,4,4,4,4,4,4,2c,2c,2c,2c,2c,2c,2d,2d,2d,2d,2d,2d,37,4,4,4,4,4,4,4,4,4,4,4,
  //   4,4,4,4,4,4,4,4,4,4,4,4,4,4,4,4,4,4,4,4,4,4,4,4,4,4,4,4,4,4,4,4,4,4,4,4,4,4,4,4,4,
  //   4,4,4,4,4,4,4,4,4,4,4,4,4,4,4,4,4,4,4,4,4,4,4,4,4,4,4,4,4,4,4,4,4,4,4,4,4,4,4,4,4,
  //   4,4,4,4,4,4,4,4,4,4,4,4,4,4,4,4,4,4,4,4,4,4,4,4,4,4,4,4,4,4,4,4,4,4,4,4,4,4,4,4,4,
  //   4,4,4,4,4,4,4,4,4,4,4,4,4,4,4,4,4,4,4,4,4,4,4,4,4,4,4,4,4,4,4,4,4,4,4,4,4,4,4,4,4,
  //   4,4,4,4,4,4,5,6,7,4,4,4,4,4,4,4,4,4,30,30,30,30,34,34,34,34,38,38,38,38,30,30,30,
  //   30,34,34,34,34,38,38,38,38,4,4,4,32,48,48,48,24,4,4,4,4,4,4,4,4,4,4,4,4,4,4,4,4,4,
  //   4,2c,2c,2c,2c,2c,2c,2d,2d,2d,2d,2d,2d,37,4,4,4,4,4,4,4,4,4,4,4,4,4,4,4,4,4,4,4,4,
  //   4,4,4,4,4,4,4,4,4,4,4,4,4,4,4,4,4,4,4,4,4,4,4,4,4,4,4,4,4,4,4,4,4,4,4,4,4,4,4,4,4,
  //   4,4,4,4,4,4,4,4,4,4,4,4,4,4,4,4,4,4,4,4,4,4,4,4,4,4,4,4,4,4,4,4,4,4,4,4,4,4,4,4,4,
  //   4,4,4,4,4,4,4,4,4,4,4,4,4,4,4,4,4,4,4,4,4,4,4,4,4,4,4,4,4,4,4,4,4,4,4,4,4,4,4,4,4,
  //   4,4,4,4,4,4,4,4,4,4,4,4,4,4,4,4,4,4,4,4,4,4,4,4,4,4,4,4,4,4,4,4,4,4,4,4,4,4,5,6,7,
  //   4,4,4,4,4,4,4,4,4,30,30,30,30,34,34,34,34,38,38,38,38,30,30,30,30,34,34,34,34,38,
  //   38,38,38,4,4,4,32,48,48,48,24,4,4,4,4,4,4,4,4,4,4,4,4,4,4,4,4,4,4,2c,2c,2c,2c,2c,
  //   2c,2d,2d,2d,2d,2d,2d,37,4,4,4,4,4,4,4,4,4,4,4,4,4,4,4,4,4,4,4,4,4,4,4,4,4,4,4,4,4,
  //   4,4,4,4,4,4,4,4,4,4,4,4,4,4,4,4,4,4,4,4,4,4,4,4,4,4,4,4,4,4,4,4,4,4,4,4,4,4,4,4,4,
  //   4,4,4,4,4,4,4,4,4,4,4,4,4,4,4,4,4,4,4,4,4,4,4,4,4,4,4,4,4,4,4,4,4,4,4,4,4,4,4,4,4,
  //   4,4,4,4,4,4,4,4,4,4,4,4,4,4,4,4,4,4,4,4,4,4,4,4,4,4,4,4,4,4,4,4,4,4,4,4,4,4,4,4,4,
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endmodule
