// Digital circuit GPR.dig as structural Verilog
module GPR (
  input  Load,
  input  A_Main,
  input  A_LHS,
  input  A_RHS,
  output [7:0] MAIN,
  output [7:0] LHS,
  output [7:0] RHS
);

  wire [7:0] Reg;

  _74541 _74541_1 (
    .pin1(A_Main), .pin2(Reg[0]), .pin3(Reg[1]), .pin4(Reg[2]), .pin5(Reg[3]), .pin6(Reg[4]), .pin7(Reg[5]),
    .pin8(Reg[6]), .pin9(Reg[7]), .pin10(1'b0), .pin11(MAIN[7]), .pin12(MAIN[6]), .pin13(MAIN[5]),
    .pin14(MAIN[4]), .pin15(MAIN[3]), .pin16(MAIN[2]), .pin17(MAIN[1]), .pin18(MAIN[0]), .pin19(1'b0),
    .pin20(1'b1));
  _74541 _74541_2 (
    .pin1(A_LHS), .pin2(Reg[0]), .pin3(Reg[1]), .pin4(Reg[2]), .pin5(Reg[3]), .pin6(Reg[4]), .pin7(Reg[5]),
    .pin8(Reg[6]), .pin9(Reg[7]), .pin10(1'b0), .pin11(LHS[7]), .pin12(LHS[6]), .pin13(LHS[5]),
    .pin14(LHS[4]), .pin15(LHS[3]), .pin16(LHS[2]), .pin17(LHS[1]), .pin18(LHS[0]), .pin19(1'b0), .pin20(1'b1));
  _74574 _74574_1 (
    .pin1(1'b0), .pin2(MAIN[0]), .pin3(MAIN[1]), .pin4(MAIN[2]), .pin5(MAIN[3]), .pin6(MAIN[4]),
    .pin7(MAIN[5]), .pin8(MAIN[6]), .pin9(MAIN[7]), .pin10(1'b0), .pin11(Load), .pin12(Reg[7]),
    .pin13(Reg[6]), .pin14(Reg[5]), .pin15(Reg[4]), .pin16(Reg[3]), .pin17(Reg[2]), .pin18(Reg[1]),
    .pin19(Reg[0]), .pin20(1'b1));
  _74541 _74541_3 (
    .pin1(A_RHS), .pin2(Reg[0]), .pin3(Reg[1]), .pin4(Reg[2]), .pin5(Reg[3]), .pin6(Reg[4]), .pin7(Reg[5]),
    .pin8(Reg[6]), .pin9(Reg[7]), .pin10(1'b0), .pin11(RHS[7]), .pin12(RHS[6]), .pin13(RHS[5]),
    .pin14(RHS[4]), .pin15(RHS[3]), .pin16(RHS[2]), .pin17(RHS[1]), .pin18(RHS[0]), .pin19(1'b0), .pin20(1'b1));

  // Other names for the same wires on the sheet: MainBus[7:0] = MAIN; LHSBus[7:0] = LHS; RHSBus[7:0] = RHS

  // Notes on the sheet:
  //   Load: default 1
  //   A_Main: default 1
  //   A_LHS: default 1
  //   A_RHS: default 1
endmodule
