// Digital circuit Main.dig as structural Verilog
module Main (
  input  Clock
);

  wire [1:0] Control_p10, Control_p10_2, Stage_1_fetch_suppress;
  wire [2:0] Control_p12, undriven_3;
  wire [3:0] Control_p11, Control_p14, Control_p15, Control_p16, Stage_1_alu_ops, undriven_2, undriven_4;
  wire [6:0] Control_p1, Control_p2, Control_p3, Control_p4, Control_p5, Control_p7, Control_p9, Control_p13;
  wire [7:0] Control_p6, Fetch_pipeout, gpr_1_lhs, gpr_1_rhs, memory_1_mem, Stage_1_pipeout,
       tranfer_register_1_main, undriven;
  wire [15:0] address_register_1_addr, tranfer_register_1_xfer;

  Address_Register address_register_1 (
    .xfer(tranfer_register_1_xfer), .ADDR(address_register_1_addr), .Control(Control_p1));  // open: I
  Address_Register address_register_2 (
    .xfer(tranfer_register_1_xfer), .ADDR(address_register_1_addr), .Control(Control_p2));  // open: I
  Address_Register address_register_3 (
    .xfer(tranfer_register_1_xfer), .ADDR(address_register_1_addr), .Control(Control_p3));  // open: I
  Address_Register address_register_4 (
    .xfer(tranfer_register_1_xfer), .ADDR(address_register_1_addr), .Control(Control_p4));  // open: I
  Address_Register address_register_5 (
    .xfer(tranfer_register_1_xfer), .ADDR(address_register_1_addr), .Control(Control_p5));  // open: I
  Tranfer_Register tranfer_register_1 (
    .MAIN(tranfer_register_1_main), .XFER(tranfer_register_1_xfer), .ADDR(address_register_1_addr),
    .Control(undriven));
  Memory memory_1 (.ADDR(address_register_1_addr), .Control(undriven_2), .MEM(memory_1_mem));
  // Probe ADDR on address_register_1_addr
  // Probe XFER on tranfer_register_1_xfer
  // Probe MEM on memory_1_mem
  // Bus_Control Control: pin names not known; wires that end beside it: Control_p1, Control_p2, Control_p3, Control_p4, Control_p5, Control_p6, Control_p7, Clock, Control_p9[6], {Control_p10_2, Control_p10}, Control_p11, Control_p12, Control_p13, Control_p14, Control_p15, Control_p16
  GPR gpr_1 (.RHS(gpr_1_rhs), .LHS(gpr_1_lhs), .MAIN(tranfer_register_1_main), .Control(Control_p14));  // open: I
  GPR gpr_2 (.RHS(gpr_1_rhs), .LHS(gpr_1_lhs), .MAIN(tranfer_register_1_main), .Control(Control_p15));  // open: I
  GPR gpr_3 (.RHS(gpr_1_rhs), .LHS(gpr_1_lhs), .MAIN(tranfer_register_1_main), .Control(Control_p16));  // open: I
  GPR gpr_4 (.RHS(gpr_1_rhs), .LHS(gpr_1_lhs), .MAIN(tranfer_register_1_main), .Control(undriven_4));  // open: I
  Constant_Register constant_register_1 (
    .MEM(memory_1_mem), .MAIN(tranfer_register_1_main), .Control(undriven_3));  // open: I
  Memory_Bridge memory_bridge_1 (.MAIN(tranfer_register_1_main), .MEM(memory_1_mem), .Control(undriven_2));
  // Probe LHS on gpr_1_lhs
  // Probe RHS on gpr_1_rhs
  // Probe MAIN on tranfer_register_1_main
  ALU alu_1 (
    .Assert_Main(Control_p13[0]), .FLAGS(Control_p9[4:0]), .LHS(gpr_1_lhs), .RHS(gpr_1_rhs),
    .MAIN(gpr_1_lhs), .Clock(Clock), .Control(Stage_1_alu_ops));
  Stage_2 Stage_2 (
    .Flags(Control_p9), .Clock(Clock), .PipeIn(Stage_1_pipeout), .Main(Control_p6), .SPSIDI(Control_p10_2),
    .Addr(Control_p12), .Bus_Request(Stage_1_fetch_suppress[1]), .PCRA_Flip(Control_p9[5]));  // open: Break
  Stage_1 Stage_1 (
    .ALU_Bus(Control_p11), .ALU_Ops(Stage_1_alu_ops), .Xfer(Control_p7),
    .Fetch_suppress(Stage_1_fetch_suppress[0]), .Control(Stage_1_fetch_suppress), .PipeOut(Stage_1_pipeout),
    .Flags(Control_p9), .Clock(Clock), .PipeIn(Fetch_pipeout));
  Fetch Fetch (
    .MEM(memory_1_mem), .Flags(Control_p9), .Clock(Clock), .PCRA(Control_p10),
    .Control(Stage_1_fetch_suppress), .PipeOut(Fetch_pipeout));
  Button #(.activeLow("true")) Reset (.out(Control_p9[6]));

  // Notes on the sheet:
  //   Clock: Hz: 10
  //   contents of ROM (hex, n*v repeats v):
  //   0,5,6d,6,1,5c,0,5,44,6,1,27,5,a9,6,1,5c,0,5,6,6,1,5c,0,5,0,6,81,29,2,2,ea,a1,6,80, 14,48,0,
  //   5,5a,6,0,fc,5f,66,7,5,95,6,2,5c,0,5,81,6,1,5c,0,5,a9,6,1,5c,0,5,59,6,1,27, 5,a9,6,1,5c,0,6,
  //   80,13,54,88,5,4b,6,0,5f,68,7e,7,7e,a2,5,20,6,0,a1,5f,68,5,0,6,82, 56,0,2,1,e8,5,81,6,1,5c,0,
  //   5,64,6,1,27,5,a9,6,1,5c,0,5,d6,6,2,5c,0,5,a9,6,1,5c,0,1, 2d,38,1,ff,5,d6,6,2,5c,0,5,a9,6,1,
  //   5c,0,a0,73,0,5,6,6,1,5c,0,5,0,6,82,4a,0,5,0,6,81, 0,27,29,5b,a,5b,0,6,80,14,54,8b,5,b2,6,0,
  //   5f,68,7,7e,36,5,ae,6,0,c2,5f,66,79,e8,a0, 6,80,13,4a,fe,5,f2,6,0,5f,66,5,d6,6,2,5c,0,5,81,6,
  //   1,5c,0,5,a9,6,1,5c,0,5,59,6,1,27, 5,a9,6,1,5c,0,a0,5,c9,6,0,5f,68,5,6a,6,0,a1,5f,68,5,4,6,1,
  //   5f,60,5,0,6,80,72,73,74, 29,5,15,6,1,e8,3,20,7e,7e,7e,7e,7e,7e,7e,7e,c2,5f,66,7a,79,78,5e,0,
  //   0,0,0,0,0,0,0, 0,0,0,0,30,31,32,33,34,35,36,37,38,39,41,42,43,44,45,46,80,c0,94,d4,53,69,65,
  //   76,65, 4f,66,20,45,72,61,74,6f,73,74,68,65,6e,65,73,0,20,69,73,20,70,72,69,6d,65,21,0,53, 69,
  //   65,76,69,6e,67,20,0,1,38,37,1,e,37,1,6,37,1,1,37,5,1,6,82,e8,54,5e,0,72,73,2,3, 5,1,6,82,48,
  //   0,a0,c4,54,0,5,9c,6,1,5f,66,1,1,37,79,78,5e,0,5,40,6,1,1c,88,13,48,37, 79,78,5e,0,2a,72,76,
  //   77,0,5,b7,6,1,29,5,c3,6,1,5b,fc,5f,65,38,5b,fc,5f,65,38,5f,71, 7d,7c,78,29,5e,0,72,73,2,f,c4,
  //   5,30,6,1,20,88,13,48,38,79,78,5e,0,5,30,6,1,72,74,75, 72,1e,3,f,84,84,84,84,c5,8a,13,48,38,
  //   78,c5,8a,13,48,38,7b,7a,78,5e,0,5,30,6,1,72, 73,74,75,72,1e,3,f,7,84,84,84,84,c5,c8,8a,8d,13,
  //   48,38,14,48,38,78,a,84,84,84,84,c5, c8,8a,8d,13,48,38,14,48,38,7b,7a,79,78,5e,0,fd,5,66,6,2,
  //   5f,65,72,7,eb,e9,80,83,fb, 58,2f,80,83,fb,58,2f,80,83,fb,58,2f,80,83,fb,58,2f,80,83,fb,58,2f,
  //   80,83,fb,58,2f, 80,83,fb,58,2f,80,83,fb,58,2f,78,0,5,67,6,2,5f,60,eb,73,e9,80,83,fb,58,2f,80,
  //   83,fb, 58,2f,80,83,fb,58,2f,80,83,fb,58,2f,80,83,fb,58,2f,80,83,fb,58,2f,80,83,fb,58,2f, 80,
  //   83,fb,58,2f,7,79,5e,0,5,8,6,82,27,24,76,77,2a,76,77,75,74,73,72,e9,4d,0,3,a,2, 30,5,66,6,2,
  //   29,5,c4,6,2,f1,5f,68,5d,0,92,32,4f,f1,5f,68,5d,0,92,32,4f,88,32,4c,0, 78,79,7a,7b,7d,7c,0,29,
  //   7d,7c,0,23,5e,0,5,8,6,82,27,24,76,77,2a,76,77,75,74,73,72, ea,4e,0,3,a,5,2b,6,2,29,5,20,6,3,
  //   fd,5f,65,5d,0,3,30,93,32,4f,0,3,a,5,20,6,3,fd,5f, 65,5d,0,3,30,93,32,4f,0,3,a,5,20,6,3,fd,5f,
  //   65,5d,0,2,30,92,32,4f,0,2,30,5,66,6,2, 29,5,3b,6,3,f1,5f,68,5d,0,92,32,4f,f1,5f,68,5d,0,92,
  //   32,4f,88,32,4c,78,79,7a,7b,7d, 7c,0,29,7d,7c,0,23,5e,0,73,ea,59,12,5a,a7,82,83,59,0,5a,a7,82,
  //   83,59,0,5a,a7,82,83, 59,0,5a,a7,82,83,59,0,5a,a7,82,83,59,0,5a,a7,82,83,59,0,5a,a7,82,83,59,
  //   0,5a,a7,79, 5e
  //   contents of Stage 1-B (hex, n*v repeats v):
  //   0,88,88,88,88,88,88,0,0,0,0,0,0,0,0,0,0,0,0,0,0,0,0,0,0,0,0,0,0,0,0,0,0,0,0,62,26, 63,36,64,
  //   46,65,56,45,54,34,35,0,a,b,c,d,0,0,0,0,0,0,0,0,0,0,0,0,0,0,0,0,0,0,0,0,0, 0,0,0,0,0,0,0,0,0,
  //   0,0,0,0,0,0,0,0,0,0,62,52,0,0,61,0,61,0,61,0,61,0,61,0,61,0,61, 0,61,0,61,51,b,b,b,b,b,b,0,
  //   0,0,0,0,0,0,0,0,0,0,0,0,0,0,0,0,0,0,0,0,0,0,0,0,0,0,0, 0,0,0,0,0,0,0,0,0,0,0,0,0,0,0,0,0,0,
  //   0,0,0,0,0,0,0,0,0,0,0,0,0,0,0,0,0,0,0,0,0,0,0, 0,0,0,0,0,0,0,0,0,0,0,0,0,0,0,0,0,0,0,0,0,0,
  //   0,0,0,0,0,0,0,0,0,0,0,0,0,0,0,0,0,0,0, 0,0,0,0,0,0,0,0,0,0,0,0,0,0,0,0,0,0,0,0,0,0,0,0,0,0,
  //   0,88,88,88,88,88,88,0,0,0,0,0, 0,0,0,0,0,0,0,0,0,0,0,0,0,0,0,0,0,0,0,0,0,0,0,62,26,63,36,64,
  //   46,65,56,45,54,34,35, 0,a,b,c,d,0,0,0,0,0,0,0,0,0,0,0,0,0,0,0,0,0,0,0,0,0,0,0,0,0,0,0,0,0,0,
  //   0,0,0,0,0,0, 0,0,0,0,62,52,0,0,61,61,0,0,61,0,61,0,61,0,61,61,0,61,61,0,61,51,b,b,b,b,b,b,0,
  //   0, 0,0,0,0,0,0,0,0,0,0,0,0,0,0,0,0,0,0,0,0,0,0,0,0,0,0,0,0,0,0,0,0,0,0,0,0,0,0,0,0,0, 0,0,0,
  //   0,0,0,0,0,0,0,0,0,0,0,0,0,0,0,0,0,0,0,0,0,0,0,0,0,0,0,0,0,0,0,0,0,0,0,0,0,0, 0,0,0,0,0,0,0,
  //   0,0,0,0,0,0,0,0,0,0,0,0,0,0,0,0,0,0,0,0,0,0,0,0,0,0,0,0,0,0,0,0,0,0, 0,0,0,0,0,0,0,0,0,0,0,
  //   0,88,88,88,88,88,88,0,0,0,0,0,0,0,0,0,0,0,0,0,0,0,0,0,0,0,0, 0,0,0,0,0,0,0,0,62,26,63,36,64,
  //   46,65,56,45,54,34,35,0,a,b,c,d,0,0,0,0,0,0,0,0,0,0, 0,0,0,0,0,0,0,0,0,0,0,0,0,0,0,0,0,0,0,0,
  //   0,0,0,0,0,0,0,0,0,0,62,52,0,0,61,0,61,61, 0,0,61,0,61,0,61,61,0,61,0,0,61,51,b,b,b,b,b,b,0,
  //   0,0,0,0,0,0,0,0,0,0,0,0,0,0,0,0, 0,0,0,0,0,0,0,0,0,0,0,0,0,0,0,0,0,0,0,0,0,0,0,0,0,0,0,0,0,
  //   0,0,0,0,0,0,0,0,0,0,0,0, 0,0,0,0,0,0,0,0,0,0,0,0,0,0,0,0,0,0,0,0,0,0,0,0,0,0,0,0,0,0,0,0,0,
  //   0,0,0,0,0,0,0,0, 0,0,0,0,0,0,0,0,0,0,0,0,0,0,0,0,0,0,0,0,0,0,0,0,0,0,0,0,0,0,0,0,0,0,0,0,0,
  //   0,88,88, 88,88,88,88,0,0,0,0,0,0,0,0,0,0,0,0,0,0,0,0,0,0,0,0,0,0,0,0,0,0,0,0,62,26,63,36,64,
  //    46,65,56,45,54,34,35,0,a,b,c,d,0,0,0,0,0,0,0,0,0,0,0,0,0,0,0,0,0,0,0,0,0,0,0,0,0, 0,0,0,0,
  //   0,0,0,0,0,0,0,0,0,0,0,62,52,0,0,61,61,0,61,0,0,61,0,61,0,61,0,61,0,0,0,61, 51,b,b,b,b,b,b,0,
  //   0,0,0,0,0,0,0,0,0,0,0,0,0,0,0,0,0,0,0,0,0,0,0,0,0,0,0,0,0,0,0,0, 0,0,0,0,0,0,0,0,0,0,0,0,0,
  //   0,0,0,0,0,0,0,0,0,0,0,0,0,0,0,0,0,0,0,0,0,0,0,0,0,0,0,0, 0,0,0,0,0,0,0,0,0,0,0,0,0,0,0,0,0,
  //   0,0,0,0,0,0,0,0,0,0,0,0,0,0,0,0,0,0,0,0,0,0,0,0, 0,0,0,0,0,0,0,0,0,0,0,0,0,0,0,0,0,0,0,0,0,
  //   0,88,88,88,88,88,88,0,0,0,0,0,0,0,0,0,0, 0,0,0,0,0,0,0,0,0,0,0,0,0,0,0,0,0,0,62,26,63,36,64,
  //   46,65,56,45,54,34,35,0,a,b,c,d, 0,0,0,0,0,0,0,0,0,0,0,0,0,0,0,0,0,0,0,0,0,0,0,0,0,0,0,0,0,0,
  //   0,0,0,0,0,0,0,0,0,0,62, 52,0,0,61,0,61,0,61,61,0,0,61,61,0,0,61,61,0,0,61,51,b,b,b,b,b,b,0,
  //   0,0,0,0,0,0,0, 0,0,0,0,0,0,0,0,0,0,0,0,0,0,0,0,0,0,0,0,0,0,0,0,0,0,0,0,0,0,0,0,0,0,0,0,0,0,
  //   0,0,0, 0,0,0,0,0,0,0,0,0,0,0,0,0,0,0,0,0,0,0,0,0,0,0,0,0,0,0,0,0,0,0,0,0,0,0,0,0,0,0,0,0, 0,
  //   0,0,0,0,0,0,0,0,0,0,0,0,0,0,0,0,0,0,0,0,0,0,0,0,0,0,0,0,0,0,0,0,0,0,0,0,0,0,0,0, 0,0,0,0,0,
  //   0,88,88,88,88,88,88,0,0,0,0,0,0,0,0,0,0,0,0,0,0,0,0,0,0,0,0,0,0,0,0,0,0, 0,0,62,26,63,36,64,
  //   46,65,56,45,54,34,35,0,a,b,c,d,0,0,0,0,0,0,0,0,0,0,0,0,0,0,0,0, 0,0,0,0,0,0,0,0,0,0,0,0,0,0,
  //   0,0,0,0,0,0,0,0,0,0,62,52,0,0,61,61,0,0,61,61,0,0,61, 61,0,61,0,61,0,0,61,51,b,b,b,b,b,b,0,
  //   0,0,0,0,0,0,0,0,0,0,0,0,0,0,0,0,0,0,0,0,0,0, 0,0,0,0,0,0,0,0,0,0,0,0,0,0,0,0,0,0,0,0,0,0,0,
  //   0,0,0,0,0,0,0,0,0,0,0,0,0,0,0,0,0,0, 0,0,0,0,0,0,0,0,0,0,0,0,0,0,0,0,0,0,0,0,0,0,0,0,0,0,0,
  //   0,0,0,0,0,0,0,0,0,0,0,0,0,0, 0,0,0,0,0,0,0,0,0,0,0,0,0,0,0,0,0,0,0,0,0,0,0,0,0,0,0,0,0,0,0,
  //   0,88,88,88,88,88,88, 0,0,0,0,0,0,0,0,0,0,0,0,0,0,0,0,0,0,0,0,0,0,0,0,0,0,0,0,62,26,63,36,64,
  //   46,65,56,45, 54,34,35,0,a,b,c,d,0,0,0,0,0,0,0,0,0,0,0,0,0,0,0,0,0,0,0,0,0,0,0,0,0,0,0,0,0,0,
  //   0, 0,0,0,0,0,0,0,0,0,62,52,0,0,61,0,61,61,0,61,0,0,61,61,0,61,0,61,0,0,61,51,b,b,b,b, b,b,0,
  //   0,0,0,0,0,0,0,0,0,0,0,0,0,0,0,0,0,0,0,0,0,0,0,0,0,0,0,0,0,0,0,0,0,0,0,0,0,0, 0,0,0,0,0,0,0,
  //   0,0,0,0,0,0,0,0,0,0,0,0,0,0,0,0,0,0,0,0,0,0,0,0,0,0,0,0,0,0,0,0,0,0, 0,0,0,0,0,0,0,0,0,0,0,
  //   0,0,0,0,0,0,0,0,0,0,0,0,0,0,0,0,0,0,0,0,0,0,0,0,0,0,0,0,0,0, 0,0,0,0,0,0,0,0,0,0,0,0,0,0,0,
  //   0,88,88,88,88,88,88,0,0,0,0,0,0,0,0,0,0,0,0,0,0,0,0, 0,0,0,0,0,0,0,0,0,0,0,0,62,26,63,36,64,
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  //   contents of Stage 2-A (hex, n*v repeats v):
  //   0,15,25,35,45,65,75,12,13,14,21,23,24,31,32,34,41,42,43,61,62,63,64,71,72,73,74,16, 26,36,46,
  //   17,27,37,47,0,0,0,0,0,0,0,0,0,0,0,0,0,0,0,0,0,0,0,0,e1,d1,0,0,0,0,0,0,0, 1f,2f,3f,4f,1f,2f,
  //   3f,4f,1f,2f,3f,4f,f1,f2,f3,f4,f1,f2,f3,f4,f1,f2,f3,f4,0,0,0,0,0, 0,0,0,0,0,0,0,0,0,0,0,0,0,
  //   0,0,0,0,0,0,0,0,f1,f2,f3,f4,f6,f7,1f,2f,3f,4f,6f,7f,0,0, 18,28,38,48,18,28,38,48,18,18,18,28,
  //   28,28,38,38,38,48,48,48,18,18,18,28,28,28,38, 38,38,48,48,48,18,28,38,48,18,28,38,48,18,18,
  //   18,28,28,28,38,38,38,48,48,48,18,18, 18,28,28,28,38,38,38,48,48,48,18,28,38,48,18,18,18,28,
  //   28,28,38,38,38,48,48,48,18, 18,18,28,28,28,38,38,38,48,48,48,18,18,18,28,28,28,38,38,38,48,
  //   48,48,18,28,38,48, 18,28,38,48,0,0,0,0,0,0,0,0,0,0,0,0,0,0,0,0,0,15,25,35,45,65,75,12,13,14,
  //   21,23,24, 31,32,34,41,42,43,61,62,63,64,71,72,73,74,16,26,36,46,17,27,37,47,0,0,0,0,0,0,0,0,
  //    0,0,0,0,0,0,0,0,0,0,0,0,e1,d1,0,0,0,0,0,0,0,1f,2f,3f,4f,1f,2f,3f,4f,1f,2f,3f,4f,f1, f2,f3,
  //   f4,f1,f2,f3,f4,f1,f2,f3,f4,0,0,0,0,0,0,0,0,0,0,0,0,0,0,0,0,0,0,0,0,0,0,0,0, 0,0,f1,f2,f3,f4,
  //   f6,f7,1f,2f,3f,4f,6f,7f,0,0,18,28,38,48,18,28,38,48,18,18,18,28,28, 28,38,38,38,48,48,48,18,
  //   18,18,28,28,28,38,38,38,48,48,48,18,28,38,48,18,28,38,48, 18,18,18,28,28,28,38,38,38,48,48,
  //   48,18,18,18,28,28,28,38,38,38,48,48,48,18,28,38, 48,18,18,18,28,28,28,38,38,38,48,48,48,18,
  //   18,18,28,28,28,38,38,38,48,48,48,18,18, 18,28,28,28,38,38,38,48,48,48,18,28,38,48,18,28,38,
  //   48,0,0,0,0,0,0,0,0,0,0,0,0,0,0, 0,0,0,15,25,35,45,65,75,12,13,14,21,23,24,31,32,34,41,42,43,
  //   61,62,63,64,71,72,73, 74,16,26,36,46,17,27,37,47,0,0,0,0,0,0,0,0,0,0,0,0,0,0,0,0,0,0,0,0,e1,
  //   d1,0,0,0,0, 0,0,0,1f,2f,3f,4f,1f,2f,3f,4f,1f,2f,3f,4f,f1,f2,f3,f4,f1,f2,f3,f4,f1,f2,f3,f4,0,
  //   0, 0,0,0,0,0,0,0,0,0,0,0,0,0,0,0,0,0,0,0,0,0,0,0,0,f1,f2,f3,f4,f6,f7,1f,2f,3f,4f,6f, 7f,0,0,
  //   18,28,38,48,18,28,38,48,18,18,18,28,28,28,38,38,38,48,48,48,18,18,18,28,28, 28,38,38,38,48,
  //   48,48,18,28,38,48,18,28,38,48,18,18,18,28,28,28,38,38,38,48,48,48, 18,18,18,28,28,28,38,38,
  //   38,48,48,48,18,28,38,48,18,18,18,28,28,28,38,38,38,48,48, 48,18,18,18,28,28,28,38,38,38,48,
  //   48,48,18,18,18,28,28,28,38,38,38,48,48,48,18,28, 38,48,18,28,38,48,0,0,0,0,0,0,0,0,0,0,0,0,
  //   0,0,0,0,0,15,25,35,45,65,75,12,13,14,21, 23,24,31,32,34,41,42,43,61,62,63,64,71,72,73,74,16,
  //   26,36,46,17,27,37,47,0,0,0,0,0, 0,0,0,0,0,0,0,0,0,0,0,0,0,0,0,e1,d1,0,0,0,0,0,0,0,1f,2f,3f,
  //   4f,1f,2f,3f,4f,1f,2f,3f, 4f,f1,f2,f3,f4,f1,f2,f3,f4,f1,f2,f3,f4,0,0,0,0,0,0,0,0,0,0,0,0,0,0,
  //   0,0,0,0,0,0,0, 0,0,0,0,0,f1,f2,f3,f4,f6,f7,1f,2f,3f,4f,6f,7f,0,0,18,28,38,48,18,28,38,48,18,
  //   18,18, 28,28,28,38,38,38,48,48,48,18,18,18,28,28,28,38,38,38,48,48,48,18,28,38,48,18,28, 38,
  //   48,18,18,18,28,28,28,38,38,38,48,48,48,18,18,18,28,28,28,38,38,38,48,48,48,18, 28,38,48,18,
  //   18,18,28,28,28,38,38,38,48,48,48,18,18,18,28,28,28,38,38,38,48,48,48, 18,18,18,28,28,28,38,
  //   38,38,48,48,48,18,28,38,48,18,28,38,48,0,0,0,0,0,0,0,0,0,0,0, 0,0,0,0,0,0,15,25,35,45,65,75,
  //   12,13,14,21,23,24,31,32,34,41,42,43,61,62,63,64,71, 72,73,74,16,26,36,46,17,27,37,47,0,0,0,
  //   0,0,0,0,0,0,0,0,0,0,0,0,0,0,0,0,0,e1,d1,0, 0,0,0,0,0,0,1f,2f,3f,4f,1f,2f,3f,4f,1f,2f,3f,4f,
  //   f1,f2,f3,f4,f1,f2,f3,f4,f1,f2,f3, f4,0,0,0,0,0,0,0,0,0,0,0,0,0,0,0,0,0,0,0,0,0,0,0,0,0,0,f1,
  //   f2,f3,f4,f6,f7,1f,2f,3f, 4f,6f,7f,0,0,18,28,38,48,18,28,38,48,18,18,18,28,28,28,38,38,38,48,
  //   48,48,18,18,18, 28,28,28,38,38,38,48,48,48,18,28,38,48,18,28,38,48,18,18,18,28,28,28,38,38,
  //   38,48, 48,48,18,18,18,28,28,28,38,38,38,48,48,48,18,28,38,48,18,18,18,28,28,28,38,38,38, 48,
  //   48,48,18,18,18,28,28,28,38,38,38,48,48,48,18,18,18,28,28,28,38,38,38,48,48,48, 18,28,38,48,
  //   18,28,38,48,0,0,0,0,0,0,0,0,0,0,0,0,0,0,0,0,0,15,25,35,45,65,75,12,13, 14,21,23,24,31,32,34,
  //   41,42,43,61,62,63,64,71,72,73,74,16,26,36,46,17,27,37,47,0,0, 0,0,0,0,0,0,0,0,0,0,0,0,0,0,0,
  //   0,0,0,e1,d1,0,0,0,0,0,0,0,1f,2f,3f,4f,1f,2f,3f,4f,1f, 2f,3f,4f,f1,f2,f3,f4,f1,f2,f3,f4,f1,f2,
  //   f3,f4,0,0,0,0,0,0,0,0,0,0,0,0,0,0,0,0,0,0, 0,0,0,0,0,0,0,0,f1,f2,f3,f4,f6,f7,1f,2f,3f,4f,6f,
  //   7f,0,0,18,28,38,48,18,28,38,48,18, 18,18,28,28,28,38,38,38,48,48,48,18,18,18,28,28,28,38,38,
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  //   contents of Stage 2-B (hex, n*v repeats v):
  //   4,4,4,4,4,4,4,4,4,4,4,4,4,4,4,4,4,4,4,4,4,4,4,4,4,4,4,4,4,4,4,4,4,4,4,4,4,4,4,4,4, 4,4,4,4,
  //   4,4,4,4,4,4,4,5,6,7,4,4,4,4,4,4,4,4,4,30,30,30,30,34,34,34,34,38,38,38,38, 30,30,30,30,34,34,
  //   34,34,38,38,38,38,4,4,4,4,48,48,48,24,4,4,4,4,4,4,4,4,4,4,4,4,4, 4,4,4,4,4,2c,2c,2c,2c,2c,2c,
  //   2d,2d,2d,2d,2d,2d,4,4,4,4,4,4,4,4,4,4,4,4,4,4,4,4,4,4, 4,4,4,4,4,4,4,4,4,4,4,4,4,4,4,4,4,4,
  //   4,4,4,4,4,4,4,4,4,4,4,4,4,4,4,4,4,4,4,4,4,4,4, 4,4,4,4,4,4,4,4,4,4,4,4,4,4,4,4,4,4,4,4,4,4,
  //   4,4,4,4,4,4,4,4,4,4,4,4,4,4,4,4,4,4,4, 4,4,4,4,4,4,4,4,4,4,4,4,4,4,4,4,4,4,4,4,4,4,4,4,4,4,
  //   4,4,4,4,4,4,4,4,4,4,4,4,4,4,4, 4,4,4,4,4,4,4,4,4,4,4,4,4,4,4,4,4,4,4,4,4,4,4,4,4,4,4,4,4,4,
  //   4,4,4,4,4,4,4,4,4,4,4, 5,6,7,4,4,4,4,4,4,4,4,4,30,30,30,30,34,34,34,34,38,38,38,38,30,30,30,
  //   30,34,34,34, 34,38,38,38,38,4,4,4,4,48,48,48,24,4,4,4,4,4,4,4,4,4,4,4,4,4,4,4,4,4,4,2c,2c,2c,
  //   2c, 2c,2c,2d,2d,2d,2d,2d,2d,4,4,4,4,4,4,4,4,4,4,4,4,4,4,4,4,4,4,4,4,4,4,4,4,4,4,4,4,4, 4,4,
  //   4,4,4,4,4,4,4,4,4,4,4,4,4,4,4,4,4,4,4,4,4,4,4,4,4,4,4,4,4,4,4,4,4,4,4,4,4,4,4, 4,4,4,4,4,4,
  //   4,4,4,4,4,4,4,4,4,4,4,4,4,4,4,4,4,4,4,4,4,4,4,4,4,4,4,4,4,4,4,4,4,4,4, 4,4,4,4,4,4,4,4,4,4,
  //   4,4,4,4,4,4,4,4,4,4,4,4,4,4,4,4,4,4,4,4,4,4,4,4,4,4,4,4,4,4,4, 4,4,4,4,4,4,4,4,4,4,4,4,4,4,
  //   4,4,4,4,4,4,4,4,4,4,4,4,4,4,4,4,5,6,7,4,4,4,4,4,4,4,4, 4,30,30,30,30,34,34,34,34,38,38,38,38,
  //   30,30,30,30,34,34,34,34,38,38,38,38,4,4,4,4, 48,48,48,24,4,4,4,4,4,4,4,4,4,4,4,4,4,4,4,4,4,
  //   4,2c,2c,2c,2c,2c,2c,2d,2d,2d,2d,2d, 2d,4,4,4,4,4,4,4,4,4,4,4,4,4,4,4,4,4,4,4,4,4,4,4,4,4,4,
  //   4,4,4,4,4,4,4,4,4,4,4,4,4, 4,4,4,4,4,4,4,4,4,4,4,4,4,4,4,4,4,4,4,4,4,4,4,4,4,4,4,4,4,4,4,4,
  //   4,4,4,4,4,4,4,4,4, 4,4,4,4,4,4,4,4,4,4,4,4,4,4,4,4,4,4,4,4,4,4,4,4,4,4,4,4,4,4,4,4,4,4,4,4,
  //   4,4,4,4,4, 4,4,4,4,4,4,4,4,4,4,4,4,4,4,4,4,4,4,4,4,4,4,4,4,4,4,4,4,4,4,4,4,4,4,4,4,4,4,4,4,
  //   4, 4,4,4,4,4,4,4,4,4,4,4,4,4,4,4,4,4,4,4,4,5,6,7,4,4,4,4,4,4,4,4,4,30,30,30,30,34,34, 34,34,
  //   38,38,38,38,30,30,30,30,34,34,34,34,38,38,38,38,4,4,4,4,48,48,48,24,4,4,4,4, 4,4,4,4,4,4,4,
  //   4,4,4,4,4,4,4,2c,2c,2c,2c,2c,2c,2d,2d,2d,2d,2d,2d,4,4,4,4,4,4,4,4,4, 4,4,4,4,4,4,4,4,4,4,4,
  //   4,4,4,4,4,4,4,4,4,4,4,4,4,4,4,4,4,4,4,4,4,4,4,4,4,4,4,4,4,4, 4,4,4,4,4,4,4,4,4,4,4,4,4,4,4,
  //   4,4,4,4,4,4,4,4,4,4,4,4,4,4,4,4,4,4,4,4,4,4,4,4,4,4, 4,4,4,4,4,4,4,4,4,4,4,4,4,4,4,4,4,4,4,
  //   4,4,4,4,4,4,4,4,4,4,4,4,4,4,4,4,4,4,4,4,4,4, 4,4,4,4,4,4,4,4,4,4,4,4,4,4,4,4,4,4,4,4,4,4,4,
  //   4,4,4,4,4,4,4,4,4,4,4,4,4,4,4,4,4,4, 4,4,4,4,4,4,4,4,4,5,6,7,4,4,4,4,4,4,4,4,4,30,30,30,30,
  //   34,34,34,34,38,38,38,38,30, 30,30,30,34,34,34,34,38,38,38,38,4,4,4,4,48,48,48,24,4,4,4,4,4,
  //   4,4,4,4,4,4,4,4,4, 4,4,4,4,2c,2c,2c,2c,2c,2c,2d,2d,2d,2d,2d,2d,4,4,4,4,4,4,4,4,4,4,4,4,4,4,
  //   4,4,4,4,4, 4,4,4,4,4,4,4,4,4,4,4,4,4,4,4,4,4,4,4,4,4,4,4,4,4,4,4,4,4,4,4,4,4,4,4,4,4,4,4,4,
  //   4, 4,4,4,4,4,4,4,4,4,4,4,4,4,4,4,4,4,4,4,4,4,4,4,4,4,4,4,4,4,4,4,4,4,4,4,4,4,4,4,4,4, 4,4,4,
  //   4,4,4,4,4,4,4,4,4,4,4,4,4,4,4,4,4,4,4,4,4,4,4,4,4,4,4,4,4,4,4,4,4,4,4,4,4,4, 4,4,4,4,4,4,4,
  //   4,4,4,4,4,4,4,4,4,4,4,4,4,4,4,4,4,4,4,4,4,4,4,4,4,4,4,4,4,4,4,4,4,5, 6,7,4,4,4,4,4,4,4,4,4,
  //   30,30,30,30,34,34,34,34,38,38,38,38,30,30,30,30,34,34,34,34, 38,38,38,38,4,4,4,4,48,48,48,24,
  //   4,4,4,4,4,4,4,4,4,4,4,4,4,4,4,4,4,4,2c,2c,2c,2c,2c, 2c,2d,2d,2d,2d,2d,2d,4,4,4,4,4,4,4,4,4,
  //   4,4,4,4,4,4,4,4,4,4,4,4,4,4,4,4,4,4,4,4,4, 4,4,4,4,4,4,4,4,4,4,4,4,4,4,4,4,4,4,4,4,4,4,4,4,
  //   4,4,4,4,4,4,4,4,4,4,4,4,4,4,4,4,4, 4,4,4,4,4,4,4,4,4,4,4,4,4,4,4,4,4,4,4,4,4,4,4,4,4,4,4,4,
  //   4,4,4,4,4,4,4,4,4,4,4,4,4, 4,4,4,4,4,4,4,4,4,4,4,4,4,4,4,4,4,4,4,4,4,4,4,4,4,4,4,4,4,4,4,4,
  //   4,4,4,4,4,4,4,4,4, 4,4,4,4,4,4,4,4,4,4,4,4,4,4,4,4,4,4,4,4,4,4,4,4,4,4,4,4,4,5,6,7,4,4,4,4,
  //   4,4,4,4,4, 30,30,30,30,34,34,34,34,38,38,38,38,30,30,30,30,34,34,34,34,38,38,38,38,4,4,4,4,
  //   48, 48,48,24,4,4,4,4,4,4,4,4,4,4,4,4,4,4,4,4,4,4,2c,2c,2c,2c,2c,2c,2d,2d,2d,2d,2d,2d, 4,4,4,
  //   4,4,4,4,4,4,4,4,4,4,4,4,4,4,4,4,4,4,4,4,4,4,4,4,4,4,4,4,4,4,4,4,4,4,4,4,4,4, 4,4,4,4,4,4,4,
  //   4,4,4,4,4,4,4,4,4,4,4,4,4,4,4,4,4,4,4,4,4,4,4,4,4,4,4,4,4,4,4,4,4,4, 4,4,4,4,4,4,4,4,4,4,4,
  //   4,4,4,4,4,4,4,4,4,4,4,4,4,4,4,4,4,4,4,4,4,4,4,4,4,4,4,4,4,4, 4,4,4,4,4,4,4,4,4,4,4,4,4,4,4,
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  //   contents of Stage 1-A (hex, n*v repeats v):
  //   0,0,0,0,0,0,0,0,0,0,0,0,0,0,0,0,0,0,0,0,0,0,0,0,0,0,0,0,0,0,0,0,0,0,0,0,0,0,0,0,0, 0,0,0,0,
  //   0,0,0,0,0,0,0,0,0,0,0,0,0,0,0,0,0,0,0,0,0,0,0,0,0,0,0,0,0,0,0,0,0,0,0,0,0, 0,0,0,0,0,0,0,0,
  //   0,0,0,0,0,0,0,0,0,0,0,0,0,0,0,0,0,0,0,0,0,0,0,0,0,0,0,0,0,0,0,0,0, 0,0,0,0,e0,10,15,1a,1f,20,
  //   25,2a,2f,34,38,3c,31,39,3d,32,36,3e,33,37,3b,44,48,4c,41, 49,4d,42,46,4e,43,47,4b,50,55,5a,
  //   5f,60,65,6a,6f,74,78,7c,71,79,7d,72,76,7e,73,77, 7b,84,88,8c,81,89,8d,82,86,8e,83,87,8b,90,
  //   95,9a,9f,a4,a8,ac,a1,a9,ad,a2,a6,ae,a3, a7,ab,b4,b8,bc,b1,b9,bd,b2,b6,be,b3,b7,bb,c4,c8,cc,
  //   c1,c9,cd,c2,c6,ce,c3,c7,cb,c0, c5,ca,cf,d0,d5,da,df,74,78,7c,71,79,7d,72,76,7e,73,77,7b,a0,
  //   a5,aa,af,0,0,0,0,0,0, 0,0,0,0,0,0,0,0,0,0,0,0,0,0,0,0,0,0,0,0,0,0,0,0,0,0,0,0,0,0,0,0,0,0,0,
  //   0,0,0,0,0,0, 0,0,0,0,0,0,0,0,0,0,0,0,0,0,0,0,0,0,0,0,0,0,0,0,0,0,0,0,0,0,0,0,0,0,0,0,0,0,0,
  //   0,0, 0,0,0,0,0,0,0,0,0,0,0,0,0,0,0,0,0,0,0,0,0,0,0,0,0,0,0,0,0,0,0,0,0,0,0,0,0,0,0,e0, 10,15,
  //   1a,1f,20,25,2a,2f,34,38,3c,31,39,3d,32,36,3e,33,37,3b,44,48,4c,41,49,4d,42, 46,4e,43,47,4b,
  //   50,55,5a,5f,60,65,6a,6f,74,78,7c,71,79,7d,72,76,7e,73,77,7b,84,88, 8c,81,89,8d,82,86,8e,83,
  //   87,8b,90,95,9a,9f,a4,a8,ac,a1,a9,ad,a2,a6,ae,a3,a7,ab,b4, b8,bc,b1,b9,bd,b2,b6,be,b3,b7,bb,
  //   c4,c8,cc,c1,c9,cd,c2,c6,ce,c3,c7,cb,c0,c5,ca,cf, d0,d5,da,df,74,78,7c,71,79,7d,72,76,7e,73,
  //   77,7b,a0,a5,aa,af,0,0,0,0,0,0,0,0,0,0,0, 0,0,0,0,0,0,0,0,0,0,0,0,0,0,0,0,0,0,0,0,0,0,0,0,0,
  //   0,0,0,0,0,0,0,0,0,0,0,0,0,0,0,0, 0,0,0,0,0,0,0,0,0,0,0,0,0,0,0,0,0,0,0,0,0,0,0,0,0,0,0,0,0,
  //   0,0,0,0,0,0,0,0,0,0,0,0, 0,0,0,0,0,0,0,0,0,0,0,0,0,0,0,0,0,0,0,0,0,0,0,0,0,0,0,0,0,0,0,0,0,
  //   0,e0,10,15,1a,1f, 20,25,2a,2f,34,38,3c,31,39,3d,32,36,3e,33,37,3b,44,48,4c,41,49,4d,42,46,4e,
  //   43,47, 4b,50,55,5a,5f,60,65,6a,6f,74,78,7c,71,79,7d,72,76,7e,73,77,7b,84,88,8c,81,89,8d, 82,
  //   86,8e,83,87,8b,90,95,9a,9f,a4,a8,ac,a1,a9,ad,a2,a6,ae,a3,a7,ab,b4,b8,bc,b1,b9, bd,b2,b6,be,
  //   b3,b7,bb,c4,c8,cc,c1,c9,cd,c2,c6,ce,c3,c7,cb,c0,c5,ca,cf,d0,d5,da,df, 74,78,7c,71,79,7d,72,
  //   76,7e,73,77,7b,a0,a5,aa,af,0,0,0,0,0,0,0,0,0,0,0,0,0,0,0,0,0, 0,0,0,0,0,0,0,0,0,0,0,0,0,0,0,
  //   0,0,0,0,0,0,0,0,0,0,0,0,0,0,0,0,0,0,0,0,0,0,0,0,0,0, 0,0,0,0,0,0,0,0,0,0,0,0,0,0,0,0,0,0,0,
  //   0,0,0,0,0,0,0,0,0,0,0,0,0,0,0,0,0,0,0,0,0,0, 0,0,0,0,0,0,0,0,0,0,0,0,0,0,0,0,0,0,0,0,0,0,0,
  //   0,0,0,0,0,e0,10,15,1a,1f,20,25,2a,2f, 34,38,3c,31,39,3d,32,36,3e,33,37,3b,44,48,4c,41,49,4d,
  //   42,46,4e,43,47,4b,50,55,5a, 5f,60,65,6a,6f,74,78,7c,71,79,7d,72,76,7e,73,77,7b,84,88,8c,81,
  //   89,8d,82,86,8e,83, 87,8b,90,95,9a,9f,a4,a8,ac,a1,a9,ad,a2,a6,ae,a3,a7,ab,b4,b8,bc,b1,b9,bd,
  //   b2,b6,be, b3,b7,bb,c4,c8,cc,c1,c9,cd,c2,c6,ce,c3,c7,cb,c0,c5,ca,cf,d0,d5,da,df,74,78,7c,71,
  //    79,7d,72,76,7e,73,77,7b,a0,a5,aa,af,0,0,0,0,0,0,0,0,0,0,0,0,0,0,0,0,0,0,0,0,0,0,0, 0,0,0,0,
  //   0,0,0,0,0,0,0,0,0,0,0,0,0,0,0,0,0,0,0,0,0,0,0,0,0,0,0,0,0,0,0,0,0,0,0,0,0, 0,0,0,0,0,0,0,0,
  //   0,0,0,0,0,0,0,0,0,0,0,0,0,0,0,0,0,0,0,0,0,0,0,0,0,0,0,0,0,0,0,0,0, 0,0,0,0,0,0,0,0,0,0,0,0,
  //   0,0,0,0,0,0,0,0,0,0,e0,10,15,1a,1f,20,25,2a,2f,34,38,3c,31, 39,3d,32,36,3e,33,37,3b,44,48,4c,
  //   41,49,4d,42,46,4e,43,47,4b,50,55,5a,5f,60,65,6a, 6f,74,78,7c,71,79,7d,72,76,7e,73,77,7b,84,
  //   88,8c,81,89,8d,82,86,8e,83,87,8b,90,95, 9a,9f,a4,a8,ac,a1,a9,ad,a2,a6,ae,a3,a7,ab,b4,b8,bc,
  //   b1,b9,bd,b2,b6,be,b3,b7,bb,c4, c8,cc,c1,c9,cd,c2,c6,ce,c3,c7,cb,c0,c5,ca,cf,d0,d5,da,df,74,
  //   78,7c,71,79,7d,72,76, 7e,73,77,7b,a0,a5,aa,af,0,0,0,0,0,0,0,0,0,0,0,0,0,0,0,0,0,0,0,0,0,0,0,
  //   0,0,0,0,0,0, 0,0,0,0,0,0,0,0,0,0,0,0,0,0,0,0,0,0,0,0,0,0,0,0,0,0,0,0,0,0,0,0,0,0,0,0,0,0,0,
  //   0,0, 0,0,0,0,0,0,0,0,0,0,0,0,0,0,0,0,0,0,0,0,0,0,0,0,0,0,0,0,0,0,0,0,0,0,0,0,0,0,0,0,0, 0,0,
  //   0,0,0,0,0,0,0,0,0,0,0,0,0,0,e0,10,15,1a,1f,20,25,2a,2f,34,38,3c,31,39,3d,32,36, 3e,33,37,3b,
  //   44,48,4c,41,49,4d,42,46,4e,43,47,4b,50,55,5a,5f,60,65,6a,6f,74,78,7c, 71,79,7d,72,76,7e,73,
  //   77,7b,84,88,8c,81,89,8d,82,86,8e,83,87,8b,90,95,9a,9f,a4,a8, ac,a1,a9,ad,a2,a6,ae,a3,a7,ab,
  //   b4,b8,bc,b1,b9,bd,b2,b6,be,b3,b7,bb,c4,c8,cc,c1,c9, cd,c2,c6,ce,c3,c7,cb,c0,c5,ca,cf,d0,d5,
  //   da,df,74,78,7c,71,79,7d,72,76,7e,73,77,7b, a0,a5,aa,af,0,0,0,0,0,0,0,0,0,0,0,0,0,0,0,0,0,0,
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endmodule
