// Digital circuit Memory Bridge.dig as structural Verilog
module Memory_Bridge (
  input  [3:0] Control,
  output [7:0] MAIN,
  output [7:0] MEM
);

  assign MAIN = Control[0] ? MEM : 8'bz;  // Driver driver_1
  assign MEM = Control[2] ? MAIN : 8'bz;  // Driver driver_2

  // Notes on the sheet:
  //   Control: 0: Assert
  //   1: Load
  //   2: Dir
  //   3: Ack, default 1
endmodule
