// Digital circuit Stage 1.dig as structural Verilog
module Stage_1 (
  input  [1:0] Control,
  input  [6:0] Flags,
  input  Clock,
  input  [7:0] PipeIn,
  input  [6:0] Xfer,
  input  [3:0] ALU_Bus,
  output [3:0] ALU_Ops,
  output [7:0] PipeOut,
  output Fetch_suppress
);

  wire _7400_1_pin11;
  wire [7:0] _28c256_1_p11, _28c256_2_p11, _74574_1_pin19;

  _74574 _74574_1 (
    .pin1(1'b0), .pin2(PipeIn[0]), .pin3(PipeIn[1]), .pin4(PipeIn[2]), .pin5(PipeIn[3]), .pin6(PipeIn[4]),
    .pin7(PipeIn[5]), .pin8(PipeIn[6]), .pin9(PipeIn[7]), .pin10(1'b0), .pin11(Clock),
    .pin12(_74574_1_pin19[7]), .pin13(_74574_1_pin19[6]), .pin14(_74574_1_pin19[5]),
    .pin15(_74574_1_pin19[4]), .pin16(_74574_1_pin19[3]), .pin17(_74574_1_pin19[2]),
    .pin18(_74574_1_pin19[1]), .pin19(_74574_1_pin19[0]), .pin20(1'b1));
  _7400 _7400_1 (
    .pin1(1'b0), .pin2(1'b0), .pin4(1'b0), .pin5(1'b0), .pin7(1'b0), .pin9(1'b0), .pin10(1'b0),
    .pin11(_7400_1_pin11), .pin12(Control[0]), .pin13(Control[1]), .pin14(1'b1));  // open: pin3, pin6, pin8
  _7408 _7408_1 (
    .pin1(_7400_1_pin11), .pin2(_74574_1_pin19[7]), .pin3(PipeOut[7]), .pin4(_7400_1_pin11),
    .pin5(_74574_1_pin19[5]), .pin6(PipeOut[5]), .pin7(1'b0), .pin8(PipeOut[4]), .pin9(_74574_1_pin19[4]),
    .pin10(_7400_1_pin11), .pin11(PipeOut[6]), .pin12(_74574_1_pin19[6]), .pin13(_7400_1_pin11), .pin14(1'b1));
  _7408 _7408_2 (
    .pin1(_7400_1_pin11), .pin2(_74574_1_pin19[0]), .pin3(PipeOut[0]), .pin4(_7400_1_pin11),
    .pin5(_74574_1_pin19[2]), .pin6(PipeOut[2]), .pin7(1'b0), .pin8(PipeOut[3]), .pin9(_74574_1_pin19[3]),
    .pin10(_7400_1_pin11), .pin11(PipeOut[1]), .pin12(_74574_1_pin19[1]), .pin13(_7400_1_pin11), .pin14(1'b1));
  // _28c256 _28c256_1: pin names not known; wires that end beside it: Flags[6], Flags[4], PipeIn[7], PipeIn[6], PipeIn[5], PipeIn[4], PipeIn[3], PipeIn[2], PipeIn[1], PipeIn[0], _28c256_1_p11[0], _28c256_1_p11[1], _28c256_1_p11[2], 1'b0, 1'b1, 1'b1, Flags[5], Flags[0], Flags[1], Flags[3], 1'b0, Flags[2], 1'b0, _28c256_1_p11[7]
  _74574 _74574_2 (
    .pin1(1'b0), .pin2(_28c256_1_p11[0]), .pin3(_28c256_1_p11[1]), .pin4(_28c256_1_p11[2]),
    .pin5(_28c256_1_p11[3]), .pin6(_28c256_1_p11[4]), .pin7(_28c256_1_p11[5]), .pin8(_28c256_1_p11[6]),
    .pin9(_28c256_1_p11[7]), .pin10(1'b0), .pin11(Clock), .pin12(ALU_Ops[3]), .pin13(ALU_Ops[2]),
    .pin14(ALU_Ops[1]), .pin15(ALU_Ops[0]), .pin16(ALU_Bus[3]), .pin17(ALU_Bus[2]), .pin18(ALU_Bus[1]),
    .pin19(ALU_Bus[0]), .pin20(1'b1));
  // _28c256 _28c256_2: pin names not known; wires that end beside it: Flags[6], Flags[4], PipeIn[7], PipeIn[6], PipeIn[5], PipeIn[4], PipeIn[3], PipeIn[2], PipeIn[1], PipeIn[0], _28c256_2_p11[0], _28c256_2_p11[1], _28c256_2_p11[2], 1'b0, 1'b1, 1'b1, Flags[5], Flags[0], Flags[1], Flags[3], 1'b0, Flags[2], 1'b0, _28c256_2_p11[7]
  _74574 _74574_3 (
    .pin1(1'b0), .pin2(_28c256_2_p11[0]), .pin3(_28c256_2_p11[1]), .pin4(_28c256_2_p11[2]),
    .pin5(_28c256_2_p11[3]), .pin6(_28c256_2_p11[4]), .pin7(_28c256_2_p11[5]), .pin8(_28c256_2_p11[6]),
    .pin9(_28c256_2_p11[7]), .pin10(1'b0), .pin11(Clock), .pin12(Fetch_suppress), .pin13(Xfer[6]),
    .pin14(Xfer[5]), .pin15(Xfer[4]), .pin16(Xfer[3]), .pin17(Xfer[2]), .pin18(Xfer[1]), .pin19(Xfer[0]),
    .pin20(1'b1));

  // Other names for the same wires on the sheet: ControlOut[15:0] = {Fetch_suppress, Xfer, ALU_Ops, ALU_Bus};
  //   ControlIn[1:0] = Control

  // Notes on the sheet:
  //   ALU_Ops: 0: ALUOP0
  //   1: ALUOP1
  //   2: ALUOP2
  //   3: ALUOP3
  //   Control: 0: FetchSurpress
  //   1: BusRequest
  //   Flags: 0: Overflow
  //   1: Sign
  //   2: Zero
  //   3: CarryA
  //   4: CarryL
  //   5: PCRA Flip
  //   6: Reset
  //   Fetch_suppress: Fetch suppress
  //   Xfer: 0-2: Assert Xfer 0-2
  //   3-6: Load Xfer Dec 0-3
  //   ALU_Bus: 0,1: LHS0,1
  //   2,3: RHS0,1
endmodule
