// Digital circuit Stage 2.dig as structural Verilog
module Stage_2 (
  input  [6:0] Flags,
  input  Clock,
  input  [7:0] PipeIn,
  output Break,
  output [7:0] Main,
  output [1:0] SPSIDI,
  output [2:0] Addr,
  output Bus_Request,
  output PCRA_Flip
);

  wire [7:0] _74574_1_pin2, _74574_2_pin2;

  _28c256_programmable A (
    .nCE(1'b0), .nOE(1'b0), .nWE(1'b1), .VCC(1'b1), .GND(1'b0), .I_O0(_74574_1_pin2[0]),
    .I_O1(_74574_1_pin2[1]), .I_O2(_74574_1_pin2[2]), .I_O3(_74574_1_pin2[3]), .I_O4(_74574_1_pin2[4]),
    .I_O5(_74574_1_pin2[5]), .I_O6(_74574_1_pin2[6]), .I_O7(_74574_1_pin2[7]), .A0(PipeIn[0]),
    .A1(PipeIn[1]), .A2(PipeIn[2]), .A3(PipeIn[3]), .A4(PipeIn[4]), .A5(PipeIn[5]), .A6(PipeIn[6]),
    .A7(PipeIn[7]), .A8(Flags[0]), .A9(Flags[1]), .A10(Flags[2]), .A11(Flags[3]), .A12(Flags[4]),
    .A13(Flags[5]), .A14(Flags[6]));
  _74574 _74574_1 (
    .pin1(1'b0), .pin2(_74574_1_pin2[0]), .pin3(_74574_1_pin2[1]), .pin4(_74574_1_pin2[2]),
    .pin5(_74574_1_pin2[3]), .pin6(_74574_1_pin2[4]), .pin7(_74574_1_pin2[5]), .pin8(_74574_1_pin2[6]),
    .pin9(_74574_1_pin2[7]), .pin10(1'b0), .pin11(Clock), .pin12(Main[7]), .pin13(Main[6]), .pin14(Main[5]),
    .pin15(Main[4]), .pin16(Main[3]), .pin17(Main[2]), .pin18(Main[1]), .pin19(Main[0]), .pin20(1'b1));
  _28c256_programmable B (
    .nCE(1'b0), .nOE(1'b0), .nWE(1'b1), .VCC(1'b1), .GND(1'b0), .I_O0(_74574_2_pin2[0]),
    .I_O1(_74574_2_pin2[1]), .I_O2(_74574_2_pin2[2]), .I_O3(_74574_2_pin2[3]), .I_O4(_74574_2_pin2[4]),
    .I_O5(_74574_2_pin2[5]), .I_O6(_74574_2_pin2[6]), .I_O7(_74574_2_pin2[7]), .A0(PipeIn[0]),
    .A1(PipeIn[1]), .A2(PipeIn[2]), .A3(PipeIn[3]), .A4(PipeIn[4]), .A5(PipeIn[5]), .A6(PipeIn[6]),
    .A7(PipeIn[7]), .A8(Flags[0]), .A9(Flags[1]), .A10(Flags[2]), .A11(Flags[3]), .A12(Flags[4]),
    .A13(Flags[5]), .A14(Flags[6]));
  _74574 _74574_2 (
    .pin1(1'b0), .pin2(_74574_2_pin2[0]), .pin3(_74574_2_pin2[1]), .pin4(_74574_2_pin2[2]),
    .pin5(_74574_2_pin2[3]), .pin6(_74574_2_pin2[4]), .pin7(_74574_2_pin2[5]), .pin8(_74574_2_pin2[6]),
    .pin9(_74574_2_pin2[7]), .pin10(1'b0), .pin11(Clock), .pin12(Break), .pin13(PCRA_Flip),
    .pin14(Bus_Request), .pin15(Addr[2]), .pin16(Addr[1]), .pin17(Addr[0]), .pin18(SPSIDI[1]),
    .pin19(SPSIDI[0]), .pin20(1'b1));

  // Other names for the same wires on the sheet: ControlOut[15:0] = {Break, PCRA_Flip, Bus_Request, Addr, SPSIDI, Main}

  // Notes on the sheet:
  //   Flags: 0: Overflow
  //   1: Sign
  //   2: Zero
  //   3: CarryA
  //   4: CarryL
  //   5: PCRA Flip
  //   6: Reset
  //   Main: 0-3: Assert A-D
  //   4-7: Load A-D
  //   SPSIDI: 0,1: Inc SPSIDI0,1
  //   Addr: 000 Memory Ack
  //   001 PCRA0
  //   010 PCRA1
  //   011 SP
  //   100 SI
  //   101 DI
  //   111 TX
  //   Bus_Request: 1: PCRA Flip
  //   2: Break
endmodule
