// Digital circuit System.dig as structural Verilog
module System (
  input  Clock,
  input  BTN0,
  input  BTN3,
  input  BTN1,
  input  BTN2,
  input  SW0,
  input  SW1,
  input  SW2,
  input  SW3,
  output JA1,
  output JA2,
  output JA3,
  output JA4,
  output JA7,
  output JA8,
  output JA9,
  output JA10
);

  wire internal, nor_2_out, R_nW;
  wire [3:0] undriven;
  wire [7:0] D_IN, D_OUT, register_1_q;

  Register #(.Bits(8)) register_1 (.D(D_IN), .C(Clock), .Q(register_1_q));  // open: en
  // PinControl pincontrol_1: pin names not known; wires that end beside it: register_1_q[0], R_nW, R_nW, D_OUT[0], JA1
  // PinControl pincontrol_2: pin names not known; wires that end beside it: register_1_q[1], R_nW, D_OUT[1], JA2
  // PinControl pincontrol_3: pin names not known; wires that end beside it: register_1_q[2], R_nW, D_OUT[2], JA3
  // PinControl pincontrol_4: pin names not known; wires that end beside it: register_1_q[3], R_nW, D_OUT[3], JA4
  // PinControl pincontrol_5: pin names not known; wires that end beside it: register_1_q[4], R_nW, D_OUT[4], JA7
  // PinControl pincontrol_6: pin names not known; wires that end beside it: register_1_q[5], R_nW, D_OUT[5], JA8
  // PinControl pincontrol_7: pin names not known; wires that end beside it: register_1_q[6], R_nW, D_OUT[6], JA9
  // PinControl pincontrol_8: pin names not known; wires that end beside it: register_1_q[7], D_OUT[7], JA10
  BlockRAMDualPort #(.AddrBits(15), .Bits(8)) blockramdualport_1 ();  // open: A, Din, str, C, D
  ROM #(.AddrBits(14), .Bits(8)) rom_1 ();  // open: A, sel, D
  Core core_1 ();  // open: Clock, nReset, D_IN, R_nW, Addr, D_OUT
  nor nor_1 (internal, undriven[0], undriven[1], undriven[2], undriven[3]);
  nor nor_2 (nor_2_out, undriven[0], undriven[1], undriven[2], undriven[3]);

  // Other names for the same wires on the sheet: Reset = BTN0

  // Notes on the sheet:
  //   Clock: pin E3, Hz: 500
  //   BTN0: pin D9
  //   BTN3: pin B8
  //   BTN1: pin C9
  //   BTN2: pin B9
  //   SW0: pin A8
  //   SW1: pin C11
  //   SW2: pin C10
  //   SW3: pin A10
  //   JA1: pin G13
  //   JA2: pin B11
  //   JA3: pin A11
  //   JA4: pin D12
  //   JA7: pin D13
  //   JA8: pin B18
  //   JA9: pin A18
  //   JA10: pin K18
  //   Switches
  //   Buttons
  //   Pmod JA
  //   contents of rom_1 (hex, n*v repeats v):
  //   0,5,37,6,0,27,5,14,6,0,5c,0,0,0,5,1,6,0,5f,60,2a,72,76,77,0,5,22,6,0,29,5,31,6,0,
  //   5b,fc,5,31,6,0,5f,65,5,0,6,40,54,5f,71,7d,7c,78,29,5e,0,48,65,6c,6c,6f,20,57,6f,72,
  //   6c,64,21,a
endmodule
