// Digital circuit Terminal.dig as structural Verilog
module Terminal (
  input  [7:0] D,
  input  C,
  input  Load
);

  wire not_1_out, not_2_out;

  not not_1 (not_1_out, C);
  not not_2 (not_2_out, Load);
  Terminal terminal_1 (.D(D), .C(not_1_out), .en(not_2_out));
endmodule
