// Digital circuit Transfer Register.dig as structural Verilog
module Transfer_Register (
  input  [7:0] C,
  input  [15:0] XFER,
  output [7:0] MAIN,
  output [15:0] ADDR,
  output [15:0] I
);

  wire and_1_out, and_2_out, delay_1_out, xor_1_out;
  wire [7:0] multiplexer_1_out, multiplexer_2_out;

  and and_1 (and_1_out, C[0], C[6]);
  and and_2 (and_2_out, C[0], C[4]);
  xor xor_1 (xor_1_out, C[6], C[4]);
  Delay #(.delayTime(2)) delay_1 (.in(xor_1_out), .out(delay_1_out));
  Multiplexer #(.Bits(8)) multiplexer_1 (.sel(delay_1_out), .in_0(XFER[15:8]), .in_1(MAIN), .out(multiplexer_1_out));
  Multiplexer #(.Bits(8)) multiplexer_2 (.sel(delay_1_out), .in_0(XFER[7:0]), .in_1(MAIN), .out(multiplexer_2_out));
  Register #(.Bits(8)) TH (.D(multiplexer_1_out), .C(and_1_out), .en(1'b1), .Q(I[15:8]));
  Register #(.Bits(8)) TL (.D(multiplexer_2_out), .C(and_2_out), .en(1'b1), .Q(I[7:0]));
  assign XFER = ~C[2] ? I : 16'bz;  // DriverInvSel driverinvsel_1
  assign ADDR = ~C[1] ? I : 16'bz;  // DriverInvSel driverinvsel_2
  assign MAIN = ~C[7] ? I[15:8] : 8'bz;  // DriverInvSel driverinvsel_3
  assign MAIN = ~C[5] ? I[7:0] : 8'bz;  // DriverInvSel driverinvsel_4

  // Notes on the sheet:
  //   ADDR: Addr Bus
  //   C: 0: RegTX Load
  //   1: RegTX Assert Addr
  //   2: RegTX Assert Xfer
  //   3: RegTX Assert Mode
  //   4: RegTL Load
  //   5: RegTL Assert
  //   6: RegTH Load
  //   7: RegTH Assert, default 255
endmodule
